// Logisim project projeto circuitos v5.circ as structural Verilog: 16 circuits, main circuit main
module main (
  input  JOGAR,
  input  Selec_Player,
  input  [3:0] A,
  input  [3:0] B
);

  wire and_1_out, and_2_out, and_3_out, button_1_out, comparador_de_magnitude_1_a_menor_que_b,
       comparador_de_magnitude_1_b_menor_que_a, comparador_de_magnitude_1_igualdade, jurubeba_1_a,
       jurubeba_1_b, jurubeba_1_c, jurubeba_1_d, jurubeba_1_e, jurubeba_1_f, jurubeba_1_g, jurubeba_2_a,
       jurubeba_2_b, jurubeba_2_c, jurubeba_2_d, jurubeba_2_e, jurubeba_2_f, jurubeba_2_g;
  wire [3:0] multiplexador_2_1_out_4;

  jurubeba jurubeba_1 (
    ._3(B[3]), ._2(B[2]), ._1(B[1]), ._0(B[0]), .A(jurubeba_1_a), .B(jurubeba_1_b), .C(jurubeba_1_c),
    .D(jurubeba_1_d), .E(jurubeba_1_e), .F(jurubeba_1_f), .G(jurubeba_1_g));
  multiplexador_2 multiplexador_2_1 (.in_1(B), .in_2(A), .in_3(Selec_Player), .out_4(multiplexador_2_1_out_4));
  Button button_1 (.out(button_1_out));
  jurubeba jurubeba_2 (
    ._3(A[3]), ._2(A[2]), ._1(A[1]), ._0(A[0]), .A(jurubeba_2_a), .B(jurubeba_2_b), .C(jurubeba_2_c),
    .D(jurubeba_2_d), .E(jurubeba_2_e), .F(jurubeba_2_f), .G(jurubeba_2_g));
  comparador_de_magnitude comparador_de_magnitude_1 (
    .A(multiplexador_2_1_out_4), .B(button_1_out), .Igualdade(comparador_de_magnitude_1_igualdade),
    .A_menor_que_B(comparador_de_magnitude_1_a_menor_que_b),
    .B_menor_que_A(comparador_de_magnitude_1_b_menor_que_a));
  and and_1 (and_1_out, JOGAR, comparador_de_magnitude_1_igualdade);
  LED IGUAL (.in(and_1_out));
  LED NUMERO_ALE_E_MAIOR (.in(and_2_out));
  and and_2 (and_2_out, JOGAR, comparador_de_magnitude_1_a_menor_que_b);
  LED NUMERO_ALE_E_MENOR (.in(and_3_out));
  and and_3 (and_3_out, JOGAR, comparador_de_magnitude_1_b_menor_que_a);
  _7_Segment_Display u_7_segment_display_1 (
    .g(jurubeba_2_g), .f(jurubeba_2_f), .a(jurubeba_2_a), .b(jurubeba_2_b), .e(jurubeba_2_e),
    .d(jurubeba_2_d), .c(jurubeba_2_c));  // open: dp
  _7_Segment_Display u_7_segment_display_2 (
    .g(jurubeba_1_g), .f(jurubeba_1_f), .a(jurubeba_1_a), .b(jurubeba_1_b), .e(jurubeba_1_e),
    .d(jurubeba_1_d), .c(jurubeba_1_c));  // open: dp

  // Notes on the sheet:
  //   JOGADOR A
  //   JOGADOR B
endmodule

module multiplexador (
  input  in_1,
  input  in_2,
  input  in_3,
  output out_4
);

  wire and_1_out, and_2_out, not_1_out;

  not not_1 (not_1_out, in_3);
  and and_1 (and_1_out, in_1, in_3);
  and and_2 (and_2_out, in_2, not_1_out);
  or or_1 (out_4, and_1_out, and_2_out);
endmodule

module comparador_de_magnitude (
  input  [3:0] A,
  input  B,
  output Igualdade,
  output A_menor_que_B,
  output B_menor_que_A
);

  wire and_1_out, and_2_out, and_3_out, and_4_out, and_5_out, and_7_out, xnor_1_out_3, xnor_2_out_3,
       xnor_3_out_3, xnor_4_out_3;
  wire [3:0] random_1_out;

  Random #(.width(4)) random_1 (.clk(B), .out(random_1_out));  // open: next, clr
  \xnor  xnor_1 (.in_1(A[3]), .in_2(random_1_out[3]), .out_3(xnor_1_out_3));
  and and_1 (and_1_out, xnor_1_out_3, xnor_2_out_3);
  \xnor  xnor_2 (.in_1(A[2]), .in_2(random_1_out[2]), .out_3(xnor_2_out_3));
  \xnor  xnor_3 (.in_1(A[1]), .in_2(random_1_out[1]), .out_3(xnor_3_out_3));
  \xnor  xnor_4 (.in_1(A[0]), .in_2(random_1_out[0]), .out_3(xnor_4_out_3));
  and and_2 (and_2_out, ~random_1_out[0], A[0], xnor_3_out_3, xnor_2_out_3, xnor_1_out_3);  // AND_Gate
  and and_3 (and_3_out, ~random_1_out[1], A[1], xnor_2_out_3, xnor_1_out_3);  // AND_Gate
  and and_4 (and_4_out, ~random_1_out[2], A[2], xnor_1_out_3);  // AND_Gate
  and and_5 (and_5_out, ~A[2], A[3]);  // AND_Gate
  and and_6 (Igualdade, and_1_out, and_7_out);
  and and_7 (and_7_out, xnor_3_out_3, xnor_4_out_3);
  or or_1 (B_menor_que_A, and_2_out, and_3_out, and_4_out, and_5_out);
  \xnor  xnor_5 (.in_1(Igualdade), .in_2(B_menor_que_A), .out_3(A_menor_que_B));
endmodule

module \xor  (
  input  in_1,
  input  in_2,
  output out_3
);

  wire and_1_out, and_2_out, not_1_out, not_2_out;

  not not_1 (not_1_out, in_1);
  not not_2 (not_2_out, in_2);
  and and_1 (and_1_out, not_1_out, in_2);
  or or_1 (out_3, and_1_out, and_2_out);
  and and_2 (and_2_out, in_1, not_2_out);
endmodule

module multiplexador_2 (
  input  [3:0] in_1,
  input  [3:0] in_2,
  input  in_3,
  output [3:0] out_4
);

  multiplexador multiplexador_1 (.in_1(in_1[0]), .in_2(in_2[0]), .in_3(in_3), .out_4(out_4[0]));
  multiplexador multiplexador_2 (.in_1(in_1[1]), .in_2(in_2[1]), .in_3(in_3), .out_4(out_4[1]));
  multiplexador multiplexador_3 (.in_1(in_1[2]), .in_2(in_2[2]), .in_3(in_3), .out_4(out_4[2]));
  multiplexador multiplexador_4 (.in_1(in_1[3]), .in_2(in_2[3]), .in_3(in_3), .out_4(out_4[3]));
endmodule

module \xnor  (
  input  in_1,
  input  in_2,
  output out_3
);

  wire xor_1_out_3;

  \xor  xor_1 (.in_1(in_1), .in_2(in_2), .out_3(xor_1_out_3));
  not not_1 (out_3, xor_1_out_3);
endmodule

module decodificador (
  input  in_1,
  input  in_2,
  input  in_3,
  input  in_4,
  input  in_5,
  input  in_6
);

  wire not_1_out, not_2_out, not_3_out, not_4_out;

  not not_1 (not_1_out, in_3);
  not not_2 (not_2_out, in_2);
  // OR_Gate or_1 has open pins: in0=not_1_out, in3=in_4, out=open
  not not_3 (not_3_out, in_5);
  // AND_Gate and_1 has open pins: in0=not_3_out, in4=not_4_out, out=open
  not not_4 (not_4_out, in_6);
  // OR_Gate or_2 has open pins: in0=in_1, in4=not_2_out, out=open
endmodule

module TESTE_DE_DISPLAY (
  input  B,
  input  A,
  input  F,
  input  G,
  input  D,
  input  E,
  input  C,
  input  in_8
);

  _7_Segment_Display u_7_segment_display_1 (.g(G), .f(F), .a(A), .b(B), .e(E), .d(D), .c(C), .dp(in_8));
endmodule

module segmento_a (
  input  A,
  input  B,
  input  C,
  input  D,
  output out_5
);

  wire and_1_out, and_2_out, and_3_out, and_4_out, and_5_out, and_6_out;

  and and_1 (and_1_out, ~A, C);  // AND_Gate
  and and_2 (and_2_out, B, C);
  and and_3 (and_3_out, A, ~D);  // AND_Gate
  and and_4 (and_4_out, ~B, ~D);  // AND_Gate
  and and_5 (and_5_out, ~A, B, D);  // AND_Gate
  and and_6 (and_6_out, A, ~B, ~C);  // AND_Gate
  or or_1 (out_5, and_1_out, and_2_out, and_3_out, and_4_out, and_5_out, and_6_out);
endmodule

module SEGMENTO_B (
  input  A,
  input  B,
  input  C,
  input  D,
  output out_5
);

  wire and_1_out, and_2_out, and_3_out, and_4_out, and_5_out;

  and and_1 (and_1_out, ~B, ~C);  // AND_Gate
  and and_2 (and_2_out, ~B, ~D);  // AND_Gate
  and and_3 (and_3_out, ~A, ~C, ~D);  // AND_Gate
  and and_4 (and_4_out, ~A, C, D);  // AND_Gate
  and and_5 (and_5_out, A, ~C, D);  // AND_Gate
  or or_1 (out_5, and_1_out, and_2_out, and_3_out, and_4_out, and_5_out);
endmodule

module SEGMENTO_C (
  input  A,
  input  B,
  input  C,
  input  D,
  output out_5
);

  wire and_1_out, and_2_out, and_3_out, and_4_out, and_5_out;

  and and_1 (and_1_out, ~A, B);  // AND_Gate
  and and_2 (and_2_out, A, ~B);  // AND_Gate
  and and_3 (and_3_out, ~C, D);  // AND_Gate
  and and_4 (and_4_out, ~A, ~C);  // AND_Gate
  and and_5 (and_5_out, ~A, D);  // AND_Gate
  or or_1 (out_5, and_1_out, and_2_out, and_3_out, and_4_out, and_5_out);
endmodule

module SEGMENTO_D (
  input  A,
  input  B,
  input  C,
  input  D,
  output out_5
);

  wire and_1_out, and_2_out, and_3_out, and_4_out, and_5_out;

  and and_1 (and_1_out, A, ~C);  // AND_Gate
  and and_2 (and_2_out, B, C, ~D);  // AND_Gate
  and and_3 (and_3_out, ~B, C, D);  // AND_Gate
  and and_4 (and_4_out, ~A, ~B, ~D);  // AND_Gate
  and and_5 (and_5_out, B, ~C, D);  // AND_Gate
  or or_1 (out_5, and_1_out, and_2_out, and_3_out, and_4_out, and_5_out);
endmodule

module SEGMENTO_E (
  input  A,
  input  B,
  input  C,
  input  D,
  output out_5
);

  wire and_1_out, and_2_out, and_3_out, and_4_out, and_5_out;

  and and_1 (and_1_out, A, B);
  and and_2 (and_2_out, C, ~D);  // AND_Gate
  and and_3 (and_3_out, A, C);
  and and_4 (and_4_out, A, ~D);  // AND_Gate
  and and_5 (and_5_out, ~B, ~D);  // AND_Gate
  or or_1 (out_5, and_1_out, and_2_out, and_3_out, and_4_out, and_5_out);
endmodule

module SEGMENTO_F (
  input  A,
  input  B,
  input  C,
  input  D,
  output out_5
);

  wire and_1_out, and_2_out, and_3_out, and_4_out, and_5_out;

  and and_1 (and_1_out, A, ~B);  // AND_Gate
  and and_2 (and_2_out, ~C, ~D);  // AND_Gate
  and and_3 (and_3_out, B, ~D);  // AND_Gate
  and and_4 (and_4_out, A, C);
  and and_5 (and_5_out, ~A, B, ~C);  // AND_Gate
  or or_1 (out_5, and_1_out, and_2_out, and_3_out, and_4_out, and_5_out);
endmodule

module SEGMENTO_G (
  input  A,
  input  B,
  input  C,
  input  D,
  output out_5
);

  wire and_1_out, and_2_out, and_3_out, and_4_out, and_5_out;

  and and_1 (and_1_out, A, ~B);  // AND_Gate
  and and_2 (and_2_out, C, ~D);  // AND_Gate
  and and_3 (and_3_out, A, D);
  and and_4 (and_4_out, ~B, C);  // AND_Gate
  and and_5 (and_5_out, ~A, B, ~C);  // AND_Gate
  or or_1 (out_5, and_1_out, and_2_out, and_3_out, and_4_out, and_5_out);
endmodule

module jurubeba (
  input  _3,
  input  _2,
  input  _1,
  input  _0,
  output A,
  output B,
  output C,
  output D,
  output E,
  output F,
  output G
);

  segmento_a segmento_a_1 (.A(_3), .B(_2), .C(_1), .D(_0), .out_5(A));
  SEGMENTO_B segmento_b_1 (.A(_3), .B(_2), .C(_1), .D(_0), .out_5(B));
  SEGMENTO_C segmento_c_1 (.A(_3), .B(_2), .C(_1), .D(_0), .out_5(C));
  SEGMENTO_D segmento_d_1 (.A(_3), .B(_2), .C(_1), .D(_0), .out_5(D));
  SEGMENTO_E segmento_e_1 (.A(_3), .B(_2), .C(_1), .D(_0), .out_5(E));
  SEGMENTO_F segmento_f_1 (.A(_3), .B(_2), .C(_1), .D(_0), .out_5(F));
  SEGMENTO_G segmento_g_1 (.A(_3), .B(_2), .C(_1), .D(_0), .out_5(G));
endmodule
