// Logisim project projeto-2.20.circ as structural Verilog: 10 circuits, main circuit main
module main (
  input  [3:0] in_1,
  input  in_2,
  input  [3:0] in_3,
  input  [3:0] in_4,
  input  [3:0] in_5,
  input  [3:0] in_6,
  input  [3:0] in_7
);

  wire A_DEAD, ALTERNAR_O_JOGADOR, B_DEAD, CHUTAR, clk, GANHOU, GERAR, MAIOR, MENOR, RESET, STOP_A, STOP_B,
       STOPA, STOPB, tunnel;
  wire [3:0] DMA, DMB, DSA, DSB, UMA, UMB, USA, USB;

  Hex_Digit_Display hex_digit_display_1 (.value(UMA));  // open: dp
  Hex_Digit_Display hex_digit_display_2 (.value(DMA));  // open: dp
  timer timer_1 (
    .RESET(RESET), .CLK(clk), .TDM(DMB), .UM(in_3), .TUM(UMB), .DS(in_4), .TDS(DSB), .x(in_5), .TUS(USB),
    .SELEC(in_2), .DM(in_1), .stop(STOPB), .over(A_DEAD));
  Button button_1 (.out(STOP_A));
  Hex_Digit_Display hex_digit_display_3 (.value(DSA));  // open: dp
  Hex_Digit_Display hex_digit_display_4 (.value(USA));  // open: dp
  LED led_1 (.in(A_DEAD));
  timer timer_2 (
    .RESET(RESET), .CLK(clk), .TDM(DMA), .UM(in_3), .TUM(UMA), .DS(in_4), .TDS(DSA), .x(in_5), .TUS(USA),
    .SELEC(in_2), .DM(in_1), .stop(STOPA), .over(B_DEAD));
  Button button_2 (.out(GERAR));
  LED led_2 (.in(tunnel));
  LED led_3 (.in(MENOR));
  Clock clock_1 (.out(clk));
  Button button_3 (.out(CHUTAR));
  Button button_4 (.out(ALTERNAR_O_JOGADOR));
  LED led_4 (.in(tunnel));
  LED led_5 (.in(MAIOR));
  LED led_6 (.in(GANHOU));
  Button button_5 (.out(RESET));
  Hex_Digit_Display hex_digit_display_5 (.value(DMB));  // open: dp
  Hex_Digit_Display hex_digit_display_6 (.value(UMB));  // open: dp
  core_v3turbo core_v3turbo_1 (
    .CONFIRMAR(CHUTAR), .A(in_6), .B(in_7), .GERAR(GERAR), .Change(ALTERNAR_O_JOGADOR), .stop_a(STOP_A),
    .stop_b(STOP_B), .out_8(GANHOU), .X_ALE(MENOR), .X_ALE_2(MAIOR), .cor(tunnel), .stop_a_f(STOPA),
    .stop_b_f(STOPB));
  Button button_6 (.out(STOP_B));
  Hex_Digit_Display hex_digit_display_7 (.value(DSB));  // open: dp
  Hex_Digit_Display hex_digit_display_8 (.value(USB));  // open: dp
  LED led_7 (.in(B_DEAD));

  // Other names for the same wires on the sheet: dm[3:0] = in_1; ds[3:0] = in_4; JOGADA[3:0] = in_6;
  //   JOGADB[3:0] = in_7; SELECT = in_2; um[3:0] = in_3; us[3:0] = in_5

  // Notes on the sheet:
  //   in_3: pull=up
endmodule

// Timer
module timer (
  input  RESET,
  input  [3:0] DM,
  input  [3:0] UM,
  input  [3:0] DS,
  input  [3:0] x,
  input  CLK,
  input  stop,
  input  SELEC,
  output [3:0] TDM,
  output [3:0] TUM,
  output over,
  output [3:0] TDS,
  output [3:0] TUS
);

  wire a, and_1_out, and_2_out, and_7_out, b, c, comparator_1_eq, comparator_2_eq, comparator_3_eq,
       cont_d_1_s0, cont_d_1_s1, cont_d_1_s2, cont_d_1_s3, cont_d_2_s0, cont_d_2_s1, cont_d_2_s2,
       cont_d_2_s3, cont_u_1_s0, cont_u_1_s1, cont_u_1_s2, cont_u_1_s3, cont_u_2_s0, cont_u_2_s1,
       cont_u_2_s2, cont_u_2_s3, guil_1_a, guil_1_b, guil_1_c, multiplexer_5_out, or_1_out;
  wire [3:0] multiplexer_1_out, multiplexer_2_out, multiplexer_3_out, multiplexer_4_out;

  Multiplexer #(.width(4), .enable("false")) multiplexer_1 (
    .in0(DM), .out(multiplexer_1_out), .sel(SELEC));  // open: in1
  D_Flip_Flop d_ff_1 (
    .clk(b), .D(cont_u_1_s3), .Q(TUM[3]), .preset(multiplexer_2_out[3]), .reset(RESET));  // open: Qn, en
  Multiplexer #(.width(4), .enable("false")) multiplexer_2 (
    .in0(UM), .out(multiplexer_2_out), .sel(SELEC));  // open: in1
  D_Flip_Flop d_ff_2 (
    .clk(a), .D(cont_d_2_s3), .Q(TDS[3]), .preset(multiplexer_3_out[3]), .reset(RESET));  // open: Qn, en
  Multiplexer #(.width(4), .enable("false")) multiplexer_3 (
    .in0(DS), .out(multiplexer_3_out), .sel(SELEC));  // open: in1
  Multiplexer #(.width(4), .enable("false")) multiplexer_4 (
    .in0(x), .out(multiplexer_4_out), .sel(SELEC));  // open: in1
  D_Flip_Flop d_ff_3 (
    .clk(c), .D(cont_d_1_s2), .Q(TDM[2]), .preset(multiplexer_1_out[2]), .reset(RESET));  // open: Qn, en
  D_Flip_Flop d_ff_4 (
    .clk(c), .D(cont_d_1_s3), .Q(TDM[3]), .preset(multiplexer_1_out[3]), .reset(RESET));  // open: Qn, en
  D_Flip_Flop d_ff_5 (
    .clk(b), .D(cont_u_1_s2), .Q(TUM[2]), .preset(multiplexer_2_out[2]), .reset(RESET));  // open: Qn, en
  D_Flip_Flop d_ff_6 (
    .clk(a), .D(cont_d_2_s2), .Q(TDS[2]), .preset(multiplexer_3_out[2]), .reset(RESET));  // open: Qn, en
  D_Flip_Flop d_ff_7 (
    .clk(multiplexer_5_out), .D(cont_u_2_s3), .Q(TUS[3]), .preset(multiplexer_4_out[3]), .reset(RESET));  // open: Qn, en
  D_Flip_Flop d_ff_8 (
    .clk(multiplexer_5_out), .D(cont_u_2_s2), .Q(TUS[2]), .preset(multiplexer_4_out[2]), .reset(RESET));  // open: Qn, en
  D_Flip_Flop d_ff_9 (
    .clk(c), .D(cont_d_1_s1), .Q(TDM[1]), .preset(multiplexer_1_out[1]), .reset(RESET));  // open: Qn, en
  D_Flip_Flop d_ff_10 (
    .clk(b), .D(cont_u_1_s1), .Q(TUM[1]), .preset(multiplexer_2_out[1]), .reset(RESET));  // open: Qn, en
  D_Flip_Flop d_ff_11 (
    .clk(a), .D(cont_d_2_s1), .Q(TDS[1]), .preset(multiplexer_3_out[1]), .reset(RESET));  // open: Qn, en
  D_Flip_Flop d_ff_12 (
    .clk(multiplexer_5_out), .D(cont_u_2_s1), .Q(TUS[1]), .preset(multiplexer_4_out[1]), .reset(RESET));  // open: Qn, en
  D_Flip_Flop d_ff_13 (
    .clk(c), .D(cont_d_1_s0), .Q(TDM[0]), .preset(multiplexer_1_out[0]), .reset(RESET));  // open: Qn, en
  cont_d cont_d_1 (
    .Q3(TDM[3]), .Q2(TDM[2]), .Q1(TDM[1]), .Q0(TDM[0]), .S3(cont_d_1_s3), .S2(cont_d_1_s2), .S1(cont_d_1_s1),
    .S0(cont_d_1_s0));
  D_Flip_Flop d_ff_14 (
    .clk(b), .D(cont_u_1_s0), .Q(TUM[0]), .preset(multiplexer_2_out[0]), .reset(RESET));  // open: Qn, en
  cont_u cont_u_1 (
    .Q3(TUM[3]), .Q2(TUM[2]), .Q1(TUM[1]), .Q0(TUM[0]), .S3(cont_u_1_s3), .S2(cont_u_1_s2), .S1(cont_u_1_s1),
    .S0(cont_u_1_s0));
  D_Flip_Flop d_ff_15 (
    .clk(a), .D(cont_d_2_s0), .Q(TDS[0]), .preset(multiplexer_3_out[0]), .reset(RESET));  // open: Qn, en
  cont_d cont_d_2 (
    .Q3(TDS[3]), .Q2(TDS[2]), .Q1(TDS[1]), .Q0(TDS[0]), .S3(cont_d_2_s3), .S2(cont_d_2_s2), .S1(cont_d_2_s1),
    .S0(cont_d_2_s0));
  D_Flip_Flop d_ff_16 (
    .clk(multiplexer_5_out), .D(cont_u_2_s0), .Q(TUS[0]), .preset(multiplexer_4_out[0]), .reset(RESET));  // open: Qn, en
  cont_u cont_u_2 (
    .Q3(TUS[3]), .Q2(TUS[2]), .Q1(TUS[1]), .Q0(TUS[0]), .S3(cont_u_2_s3), .S2(cont_u_2_s2), .S1(cont_u_2_s1),
    .S0(cont_u_2_s0));
  Hex_Digit_Display hex_digit_display_1 (.value(TDM));  // open: dp
  Hex_Digit_Display hex_digit_display_2 (.value(TUM));  // open: dp
  Hex_Digit_Display hex_digit_display_3 (.value(TDS));  // open: dp
  Hex_Digit_Display hex_digit_display_4 (.value(TUS));  // open: dp
  and and_1 (and_1_out, ~TDM[0], ~TDM[1], ~TDM[2], ~TDM[3]);  // AND_Gate
  Comparator #(.width(4)) comparator_1 (.a(TUM), .b(4'b0000), .eq(comparator_1_eq));  // open: gt, lt
  Comparator #(.width(4)) comparator_2 (.a(TDS), .b(4'b0000), .eq(comparator_2_eq));  // open: gt, lt
  Multiplexer #(.enable("false")) multiplexer_5 (.in0(CLK), .out(multiplexer_5_out), .sel(or_1_out));  // open: in1
  or or_1 (or_1_out, stop, over);
  Comparator #(.width(4)) comparator_3 (.a(TUS), .b(4'b0000), .eq(comparator_3_eq));  // open: gt, lt
  and and_2 (and_2_out, ~comparator_2_eq, comparator_3_eq);  // AND_Gate
  guil guil_1 (
    .dm(and_1_out), .um(comparator_1_eq), .ds(comparator_2_eq), .us(comparator_3_eq), .c(guil_1_c),
    .b(guil_1_b), .a(guil_1_a));
  and and_3 (over, and_1_out, comparator_1_eq, comparator_2_eq, comparator_3_eq);
  and and_4 (a, and_7_out, ~and_2_out);  // AND_Gate
  and and_5 (c, SELEC, CLK, guil_1_c);
  and and_6 (b, SELEC, CLK, guil_1_b);
  and and_7 (and_7_out, SELEC, CLK, guil_1_a);

  // Other names for the same wires on the sheet: ada = SELEC; f = CLK

  // Notes on the sheet:
  //   DEZENA DE MINUTOS
  //   UNIDADE DE MINUTOS
  //   DEZENA DE SEGUNDOS
  //   UNIDADE DE MINUTOS
endmodule

module cont_d (
  input  Q3,
  input  Q2,
  input  Q1,
  input  Q0,
  output S3,
  output S2,
  output S1,
  output S0
);

  wire and_1_out, and_2_out, and_3_out, and_4_out, and_5_out, and_6_out, and_7_out, and_8_out, and_9_out,
       and_10_out, not_1_out, not_2_out, not_3_out, not_4_out, not_5_out, not_6_out, not_7_out, not_8_out,
       not_9_out, not_10_out;

  and and_1 (and_1_out, Q2, Q1, Q0);
  not not_1 (not_1_out, Q2);
  and and_2 (and_2_out, not_1_out, not_2_out, not_3_out);
  not not_2 (not_2_out, Q1);
  not not_3 (not_3_out, Q0);
  and and_3 (and_3_out, Q2, Q0);
  not not_4 (not_4_out, Q3);
  and and_4 (and_4_out, not_4_out, Q2, Q1);
  not not_5 (not_5_out, Q3);
  not not_6 (not_6_out, Q1);
  and and_5 (and_5_out, not_5_out, not_6_out, not_7_out);
  not not_7 (not_7_out, Q0);
  and and_6 (and_6_out, Q1, Q0);
  and and_7 (and_7_out, Q3, Q2, not_8_out);
  not not_8 (not_8_out, Q0);
  and and_8 (and_8_out, Q1, not_9_out);
  not not_9 (not_9_out, Q0);
  and and_9 (and_9_out, Q2, not_10_out);
  not not_10 (not_10_out, Q0);
  and and_10 (and_10_out, Q2, Q1);
  or or_1 (S3, and_1_out, Q3);
  or or_2 (S2, and_2_out, and_3_out, and_4_out);
  or or_3 (S1, and_5_out, and_6_out, and_7_out);
  or or_4 (S0, and_8_out, and_9_out, and_10_out, Q3);
endmodule

module cont_u (
  input  Q3,
  input  Q2,
  input  Q1,
  input  Q0,
  output S3,
  output S2,
  output S1,
  output S0
);

  wire and_1_out, and_2_out, and_3_out, and_4_out, and_5_out, and_6_out, and_7_out, and_8_out, and_9_out,
       and_10_out, and_11_out, and_12_out, and_13_out, and_14_out, not_1_out, not_2_out, not_3_out,
       not_4_out, not_5_out, not_6_out, not_7_out, not_8_out, not_9_out, not_10_out, not_11_out;

  not not_1 (not_1_out, Q3);
  not not_2 (not_2_out, Q2);
  not not_3 (not_3_out, Q1);
  not not_4 (not_4_out, Q0);
  and and_1 (and_1_out, Q2, Q0);
  and and_2 (and_2_out, Q2, Q1);
  not not_5 (not_5_out, Q1);
  and and_3 (and_3_out, Q3, not_5_out, not_6_out);
  not not_6 (not_6_out, Q0);
  and and_4 (and_4_out, Q3, Q1, Q0);
  and and_5 (and_5_out, Q1, Q0);
  and and_6 (and_6_out, Q2, not_7_out, not_8_out);
  not not_7 (not_7_out, Q1);
  not not_8 (not_8_out, Q0);
  not not_9 (not_9_out, Q1);
  and and_7 (and_7_out, Q3, not_9_out, not_10_out);
  not not_10 (not_10_out, Q0);
  and and_8 (and_8_out, Q3, Q2);
  not not_11 (not_11_out, Q0);
  and and_9 (and_9_out, Q3, Q1);
  and and_10 (and_10_out, Q3, Q2);
  and and_11 (and_11_out, not_1_out, not_2_out, not_3_out, not_4_out);
  and and_12 (and_12_out, Q3, Q0);
  and and_13 (and_13_out, Q3, Q1);
  and and_14 (and_14_out, Q3, Q2);
  or or_1 (S2, and_1_out, and_2_out, and_3_out, and_4_out);
  or or_2 (S1, and_5_out, and_6_out, and_7_out, and_8_out);
  or or_3 (S0, not_11_out, and_9_out, and_10_out);
  or or_4 (S3, and_11_out, and_12_out, and_13_out, and_14_out);
endmodule

module \xor  (
  input  in_1,
  input  in_2,
  output out_3
);

  wire and_1_out, and_2_out, not_1_out, not_2_out;

  not not_1 (not_1_out, in_1);
  not not_2 (not_2_out, in_2);
  and and_1 (and_1_out, not_1_out, in_2);
  or or_1 (out_3, and_1_out, and_2_out);
  and and_2 (and_2_out, in_1, not_2_out);
endmodule

module \xnor  (
  input  in_1,
  input  in_2,
  output out_3
);

  wire xor_1_out_3;

  not not_1 (out_3, xor_1_out_3);
  \xor  xor_1 (.in_1(in_1), .in_2(in_2), .out_3(xor_1_out_3));
endmodule

module comparador_de_magnitude (
  input  [3:0] X,
  input  bota_um_rotulo,
  output out_3,
  output X_ALE,
  output X_ALE_2
);

  wire and_1_out, and_2_out, and_3_out, and_4_out, and_5_out, and_7_out, xnor_1_out_3, xnor_2_out_3,
       xnor_3_out_3, xnor_4_out_3;
  wire [3:0] random_1_out;

  Random #(.width(4)) random_1 (.clk(bota_um_rotulo), .out(random_1_out));  // open: next, clr
  \xnor  xnor_1 (.in_1(X[3]), .in_2(random_1_out[3]), .out_3(xnor_1_out_3));
  and and_1 (and_1_out, xnor_1_out_3, xnor_2_out_3);
  \xnor  xnor_2 (.in_1(X[2]), .in_2(random_1_out[2]), .out_3(xnor_2_out_3));
  \xnor  xnor_3 (.in_1(X[1]), .in_2(random_1_out[1]), .out_3(xnor_3_out_3));
  \xnor  xnor_4 (.in_1(X[0]), .in_2(random_1_out[0]), .out_3(xnor_4_out_3));
  and and_2 (and_2_out, ~random_1_out[0], X[0], xnor_3_out_3, xnor_2_out_3, xnor_1_out_3);  // AND_Gate
  and and_3 (and_3_out, ~random_1_out[1], X[1], xnor_2_out_3, xnor_1_out_3);  // AND_Gate
  and and_4 (and_4_out, ~random_1_out[2], X[2], xnor_1_out_3);  // AND_Gate
  and and_5 (and_5_out, ~X[2], X[3]);  // AND_Gate
  and and_6 (out_3, and_1_out, and_7_out);
  and and_7 (and_7_out, xnor_3_out_3, xnor_4_out_3);
  or or_1 (X_ALE_2, and_2_out, and_3_out, and_4_out, and_5_out);
  \xnor  xnor_5 (.in_1(out_3), .in_2(X_ALE_2), .out_3(X_ALE));

  // Notes on the sheet:
  //   A
  //   B
endmodule

module core_v3turbo (
  input  CONFIRMAR,
  input  [3:0] A,
  input  [3:0] B,
  input  GERAR,
  input  Change,
  input  stop_a,
  input  stop_b,
  output out_8,
  output X_ALE,
  output X_ALE_2,
  output cor,
  output stop_a_f,
  output stop_b_f
);

  wire comparador_de_magnitude_1_out_3, comparador_de_magnitude_1_x_ale, comparador_de_magnitude_1_x_ale_2,
       d_ff_2_qn, d_ff_3_qn, d_ff_4_qn, not_1_out, not_2_out;
  wire [3:0] multiplexer_1_out;

  D_Flip_Flop d_ff_1 (.clk(Change), .D(cor), .Qn(cor));  // open: Q, preset, en, reset
  not not_1 (not_1_out, stop_a);
  not not_2 (not_2_out, stop_b);
  Multiplexer #(.width(4), .enable("false")) multiplexer_1 (.in0(A), .in1(B), .out(multiplexer_1_out), .sel(cor));
  D_Flip_Flop d_ff_2 (.clk(not_1_out), .D(d_ff_2_qn), .Q(stop_a_f), .Qn(d_ff_2_qn));  // open: preset, en, reset
  D_Flip_Flop d_ff_3 (.clk(not_2_out), .D(d_ff_3_qn), .Q(stop_b_f), .Qn(d_ff_3_qn));  // open: preset, en, reset
  comparador_de_magnitude comparador_de_magnitude_1 (
    .X(multiplexer_1_out), .bota_um_rotulo(GERAR), .X_ALE_2(comparador_de_magnitude_1_x_ale_2),
    .out_3(comparador_de_magnitude_1_out_3), .X_ALE(comparador_de_magnitude_1_x_ale));
  D_Flip_Flop d_ff_4 (.clk(CONFIRMAR), .D(d_ff_4_qn), .Qn(d_ff_4_qn));  // open: Q, preset, en, reset
  and and_1 (out_8, d_ff_4_qn, comparador_de_magnitude_1_out_3);
  and and_2 (X_ALE, d_ff_4_qn, comparador_de_magnitude_1_x_ale);
  and and_3 (X_ALE_2, d_ff_4_qn, comparador_de_magnitude_1_x_ale_2);
endmodule

module guilher (
  input  dm,
  input  um,
  input  ds,
  input  us,
  output c,
  output b,
  output a
);

  wire and_2_out, and_3_out, not_1_out, not_2_out, not_3_out, not_4_out;

  not not_1 (not_1_out, dm);
  not not_2 (not_2_out, um);
  and and_1 (b, not_2_out, ds, us);
  not not_3 (not_3_out, um);
  and and_2 (and_2_out, not_3_out, us);
  not not_4 (not_4_out, ds);
  and and_3 (and_3_out, not_4_out, us);
  and and_4 (c, not_1_out, um, ds, us);
  or or_1 (a, and_2_out, and_3_out);
endmodule

module guil (
  input  dm,
  input  um,
  input  ds,
  input  us,
  output c,
  output b,
  output a
);

  wire and_1_out, and_2_out, and_3_out, and_4_out, and_5_out, not_1_out, not_2_out, not_3_out, not_4_out,
       not_5_out, not_6_out;

  not not_1 (not_1_out, dm);
  not not_2 (not_2_out, dm);
  and and_1 (and_1_out, not_2_out, ds, us);
  not not_3 (not_3_out, um);
  and and_2 (and_2_out, not_3_out, ds, us);
  not not_4 (not_4_out, dm);
  and and_3 (and_3_out, not_4_out, us);
  not not_5 (not_5_out, um);
  and and_4 (and_4_out, not_5_out, us);
  not not_6 (not_6_out, ds);
  and and_5 (and_5_out, not_6_out, us);
  and and_6 (c, not_1_out, um, ds, us);
  or or_1 (b, and_1_out, and_2_out);
  or or_2 (a, and_3_out, and_4_out, and_5_out);
endmodule
