// Logisim project projeto-2.26.circ as structural Verilog: 14 circuits, main circuit main
module main (
  input  [3:0] in_1,
  input  in_2,
  input  [3:0] in_3,
  input  [3:0] in_4,
  input  [3:0] in_5,
  input  [3:0] in_6,
  input  [3:0] in_7,
  input  in_8,
  input  in_9
);

  wire A_DEAD, B_DEAD, clk, core_akina_hills_v8_nitro_1_igual, GANHOU, GERAR, MAIOR, MENOR, RESET,
       Reset_Placar, STOP_A, STOP_B, STOPA, STOPB, swap_a, swap_b, tunnel;
  wire [3:0] current_xa, current_xb, current_ya, current_yb, DMA, DMB, DSA, DSB, placar_a, placar_b, UMA,
       UMB, USA, USB;

  Hex_Digit_Display hex_digit_display_1 (.value(UMA));  // open: dp
  Hex_Digit_Display hex_digit_display_2 (.value(DMA));  // open: dp
  timer timer_1 (
    .RESET(RESET), .CLK(clk), .TDM(DMB), .UM(in_3), .TUM(UMB), .DS(in_4), .TDS(DSB), .x(in_5), .TUS(USB),
    .SELEC(in_2), .DM(in_1), .stop(STOPB), .over(A_DEAD));
  timer timer_2 (
    .RESET(RESET), .CLK(clk), .TDM(DMA), .UM(in_3), .TUM(UMA), .DS(in_4), .TDS(DSA), .x(in_5), .TUS(USA),
    .SELEC(in_2), .DM(in_1), .stop(STOPA), .over(B_DEAD));
  Button button_1 (.out(STOP_A));
  Hex_Digit_Display hex_digit_display_3 (.value(USA));  // open: dp
  Hex_Digit_Display hex_digit_display_4 (.value(DSA));  // open: dp
  LED led_1 (.in(A_DEAD));
  Button button_2 (.out(GERAR));
  LED led_2 (.in(tunnel));
  LED led_3 (.in(MENOR));
  Hex_Digit_Display hex_digit_display_5 (.value(placar_a));  // open: dp
  Clock clock_1 (.out(clk));
  Button button_3 (.out(in_9));
  Button button_4 (.out(in_9));
  LED led_4 (.in(tunnel));
  LED led_5 (.in(MAIOR));
  LED led_6 (.in(GANHOU));
  Hex_Digit_Display hex_digit_display_6 (.value(placar_b));  // open: dp
  Button button_5 (.out(Reset_Placar));
  Button button_6 (.out(RESET));
  Hex_Digit_Display hex_digit_display_7 (.value(UMB));  // open: dp
  Hex_Digit_Display hex_digit_display_8 (.value(DMB));  // open: dp
  core_akina_hills_v8_nitro core_akina_hills_v8_nitro_1 (
    .CONFIRMAR(in_8), .swap_y_a(swap_a), .gerar(GERAR), .a(in_6), .current_xa(current_xa),
    .swap_y__b(swap_b), .current_ya(current_ya), .b(in_7), .stop_a(STOPA), .current_yb(current_yb),
    .stop_b(STOPB), .reset_placar(Reset_Placar), .confirmar_b(in_9), .confirmar_a(in_9),
    .change_players(in_9), .maior(MENOR), .igual(core_akina_hills_v8_nitro_1_igual), .menor(MAIOR),
    .placary(placar_b), .placarx(placar_a), .stop_a_f(STOP_A), .stop_b_f(STOP_B), .current_xb(current_xb));
  Button button_7 (.out(STOP_B));
  Hex_Digit_Display hex_digit_display_9 (.value(current_xb));  // open: dp
  Hex_Digit_Display hex_digit_display_10 (.value(USB));  // open: dp
  Hex_Digit_Display hex_digit_display_11 (.value(DSB));  // open: dp
  LED led_7 (.in(B_DEAD));
  Hex_Digit_Display hex_digit_display_12 (.value(current_yb));  // open: dp

  // Other names for the same wires on the sheet: ALTERNAR_O_JOGADOR = in_9; CHUTAR = in_9; CONFIRMAR = in_8;
  //   dm[3:0] = in_1; ds[3:0] = in_4; JOGADA[3:0] = in_6; JOGADB[3:0] = in_7; SELECT = in_2; um[3:0] = in_3;
  //   us[3:0] = in_5

  // Notes on the sheet:
  //   in_3: pull=up
endmodule

// Timer
module timer (
  input  RESET,
  input  [3:0] DM,
  input  [3:0] UM,
  input  [3:0] DS,
  input  [3:0] x,
  input  CLK,
  input  stop,
  input  SELEC,
  output [3:0] TDM,
  output [3:0] TUM,
  output over,
  output [3:0] TDS,
  output [3:0] TUS
);

  wire a, and_1_out, and_2_out, and_7_out, b, c, comparator_1_eq, comparator_2_eq, comparator_3_eq,
       cont_d_1_s0, cont_d_1_s1, cont_d_1_s2, cont_d_1_s3, cont_d_2_s0, cont_d_2_s1, cont_d_2_s2,
       cont_d_2_s3, cont_u_1_s0, cont_u_1_s1, cont_u_1_s2, cont_u_1_s3, cont_u_2_s0, cont_u_2_s1,
       cont_u_2_s2, cont_u_2_s3, guil_1_a, guil_1_b, guil_1_c, multiplexer_5_out, not_1_out, or_1_out;
  wire [3:0] multiplexer_1_out, multiplexer_2_out, multiplexer_3_out, multiplexer_4_out;

  Multiplexer #(.width(4), .enable("false")) multiplexer_1 (
    .in0(DM), .out(multiplexer_1_out), .sel(SELEC));  // open: in1
  D_Flip_Flop d_ff_1 (
    .clk(b), .D(cont_u_1_s3), .Q(TUM[3]), .preset(multiplexer_2_out[3]), .en(not_1_out), .reset(RESET));  // open: Qn
  Multiplexer #(.width(4), .enable("false")) multiplexer_2 (
    .in0(UM), .out(multiplexer_2_out), .sel(SELEC));  // open: in1
  D_Flip_Flop d_ff_2 (
    .clk(a), .D(cont_d_2_s3), .Q(TDS[3]), .preset(multiplexer_3_out[3]), .en(not_1_out), .reset(RESET));  // open: Qn
  Multiplexer #(.width(4), .enable("false")) multiplexer_3 (
    .in0(DS), .out(multiplexer_3_out), .sel(SELEC));  // open: in1
  Multiplexer #(.width(4), .enable("false")) multiplexer_4 (
    .in0(x), .out(multiplexer_4_out), .sel(SELEC));  // open: in1
  D_Flip_Flop d_ff_3 (
    .clk(c), .D(cont_d_1_s3), .Q(TDM[3]), .preset(multiplexer_1_out[3]), .en(not_1_out), .reset(RESET));  // open: Qn
  D_Flip_Flop d_ff_4 (
    .clk(c), .D(cont_d_1_s2), .Q(TDM[2]), .preset(multiplexer_1_out[2]), .en(not_1_out), .reset(RESET));  // open: Qn
  D_Flip_Flop d_ff_5 (
    .clk(b), .D(cont_u_1_s2), .Q(TUM[2]), .preset(multiplexer_2_out[2]), .en(not_1_out), .reset(RESET));  // open: Qn
  D_Flip_Flop d_ff_6 (
    .clk(a), .D(cont_d_2_s2), .Q(TDS[2]), .preset(multiplexer_3_out[2]), .en(not_1_out), .reset(RESET));  // open: Qn
  D_Flip_Flop d_ff_7 (
    .clk(multiplexer_5_out), .D(cont_u_2_s3), .Q(TUS[3]), .preset(multiplexer_4_out[3]), .en(not_1_out),
    .reset(RESET));  // open: Qn
  D_Flip_Flop d_ff_8 (
    .clk(multiplexer_5_out), .D(cont_u_2_s2), .Q(TUS[2]), .preset(multiplexer_4_out[2]), .en(not_1_out),
    .reset(RESET));  // open: Qn
  D_Flip_Flop d_ff_9 (
    .clk(c), .D(cont_d_1_s1), .Q(TDM[1]), .preset(multiplexer_1_out[1]), .en(not_1_out), .reset(RESET));  // open: Qn
  D_Flip_Flop d_ff_10 (
    .clk(b), .D(cont_u_1_s1), .Q(TUM[1]), .preset(multiplexer_2_out[1]), .en(not_1_out), .reset(RESET));  // open: Qn
  D_Flip_Flop d_ff_11 (
    .clk(a), .D(cont_d_2_s1), .Q(TDS[1]), .preset(multiplexer_3_out[1]), .en(not_1_out), .reset(RESET));  // open: Qn
  D_Flip_Flop d_ff_12 (
    .clk(multiplexer_5_out), .D(cont_u_2_s1), .Q(TUS[1]), .preset(multiplexer_4_out[1]), .en(not_1_out),
    .reset(RESET));  // open: Qn
  D_Flip_Flop d_ff_13 (
    .clk(c), .D(cont_d_1_s0), .Q(TDM[0]), .preset(multiplexer_1_out[0]), .en(not_1_out), .reset(RESET));  // open: Qn
  cont_d cont_d_1 (
    .Q3(TDM[3]), .Q2(TDM[2]), .Q1(TDM[1]), .Q0(TDM[0]), .S3(cont_d_1_s3), .S2(cont_d_1_s2), .S1(cont_d_1_s1),
    .S0(cont_d_1_s0));
  D_Flip_Flop d_ff_14 (
    .clk(b), .D(cont_u_1_s0), .Q(TUM[0]), .preset(multiplexer_2_out[0]), .en(not_1_out), .reset(RESET));  // open: Qn
  cont_u cont_u_1 (
    .Q3(TUM[3]), .Q2(TUM[2]), .Q1(TUM[1]), .Q0(TUM[0]), .S3(cont_u_1_s3), .S2(cont_u_1_s2), .S1(cont_u_1_s1),
    .S0(cont_u_1_s0));
  D_Flip_Flop d_ff_15 (
    .clk(a), .D(cont_d_2_s0), .Q(TDS[0]), .preset(multiplexer_3_out[0]), .en(not_1_out), .reset(RESET));  // open: Qn
  cont_d cont_d_2 (
    .Q3(TDS[3]), .Q2(TDS[2]), .Q1(TDS[1]), .Q0(TDS[0]), .S3(cont_d_2_s3), .S2(cont_d_2_s2), .S1(cont_d_2_s1),
    .S0(cont_d_2_s0));
  D_Flip_Flop d_ff_16 (
    .clk(multiplexer_5_out), .D(cont_u_2_s0), .Q(TUS[0]), .preset(multiplexer_4_out[0]), .en(not_1_out),
    .reset(RESET));  // open: Qn
  cont_u cont_u_2 (
    .Q3(TUS[3]), .Q2(TUS[2]), .Q1(TUS[1]), .Q0(TUS[0]), .S3(cont_u_2_s3), .S2(cont_u_2_s2), .S1(cont_u_2_s1),
    .S0(cont_u_2_s0));
  Hex_Digit_Display hex_digit_display_1 (.value(TDM));  // open: dp
  Hex_Digit_Display hex_digit_display_2 (.value(TUM));  // open: dp
  Hex_Digit_Display hex_digit_display_3 (.value(TDS));  // open: dp
  Hex_Digit_Display hex_digit_display_4 (.value(TUS));  // open: dp
  and and_1 (and_1_out, ~TDM[0], ~TDM[1], ~TDM[2], ~TDM[3]);  // AND_Gate
  Comparator #(.width(4)) comparator_1 (.a(TUM), .b(4'b0000), .eq(comparator_1_eq));  // open: gt, lt
  Comparator #(.width(4)) comparator_2 (.a(TDS), .b(4'b0000), .eq(comparator_2_eq));  // open: gt, lt
  Multiplexer #(.enable("false")) multiplexer_5 (.in0(CLK), .out(multiplexer_5_out), .sel(1'b0));  // open: in1
  not not_1 (not_1_out, or_1_out);
  or or_1 (or_1_out, stop, over);
  Comparator #(.width(4)) comparator_3 (.a(TUS), .b(4'b0000), .eq(comparator_3_eq));  // open: gt, lt
  and and_2 (and_2_out, ~comparator_2_eq, comparator_3_eq);  // AND_Gate
  guil guil_1 (
    .dm(and_1_out), .um(comparator_1_eq), .ds(comparator_2_eq), .us(comparator_3_eq), .c(guil_1_c),
    .b(guil_1_b), .a(guil_1_a));
  and and_3 (over, and_1_out, comparator_1_eq, comparator_2_eq, comparator_3_eq);
  and and_4 (a, and_7_out, ~and_2_out);  // AND_Gate
  and and_5 (c, SELEC, CLK, guil_1_c);
  and and_6 (b, SELEC, CLK, guil_1_b);
  and and_7 (and_7_out, SELEC, CLK, guil_1_a);

  // Other names for the same wires on the sheet: ada = SELEC; f = CLK

  // Notes on the sheet:
  //   DEZENA DE MINUTOS
  //   UNIDADE DE MINUTOS
  //   DEZENA DE SEGUNDOS
  //   UNIDADE DE MINUTOS
endmodule

module cont_d (
  input  Q3,
  input  Q2,
  input  Q1,
  input  Q0,
  output S3,
  output S2,
  output S1,
  output S0
);

  wire and_1_out, and_2_out, and_3_out, and_4_out, and_5_out, and_6_out, and_7_out, and_8_out, and_9_out,
       and_10_out, not_1_out, not_2_out, not_3_out, not_4_out, not_5_out, not_6_out, not_7_out, not_8_out,
       not_9_out, not_10_out;

  and and_1 (and_1_out, Q2, Q1, Q0);
  not not_1 (not_1_out, Q2);
  not not_2 (not_2_out, Q1);
  and and_2 (and_2_out, not_1_out, not_2_out, not_3_out);
  not not_3 (not_3_out, Q0);
  and and_3 (and_3_out, Q2, Q0);
  not not_4 (not_4_out, Q3);
  and and_4 (and_4_out, not_4_out, Q2, Q1);
  not not_5 (not_5_out, Q3);
  and and_5 (and_5_out, not_5_out, not_6_out, not_7_out);
  not not_6 (not_6_out, Q1);
  not not_7 (not_7_out, Q0);
  and and_6 (and_6_out, Q1, Q0);
  and and_7 (and_7_out, Q3, Q2, not_8_out);
  not not_8 (not_8_out, Q0);
  and and_8 (and_8_out, Q1, not_9_out);
  not not_9 (not_9_out, Q0);
  and and_9 (and_9_out, Q2, not_10_out);
  not not_10 (not_10_out, Q0);
  and and_10 (and_10_out, Q2, Q1);
  or or_1 (S3, and_1_out, Q3);
  or or_2 (S2, and_2_out, and_3_out, and_4_out);
  or or_3 (S1, and_5_out, and_6_out, and_7_out);
  or or_4 (S0, and_8_out, and_9_out, and_10_out, Q3);
endmodule

module cont_u (
  input  Q3,
  input  Q2,
  input  Q1,
  input  Q0,
  output S3,
  output S2,
  output S1,
  output S0
);

  wire and_1_out, and_2_out, and_3_out, and_4_out, and_5_out, and_6_out, and_7_out, and_8_out, and_9_out,
       and_10_out, and_11_out, and_12_out, and_13_out, and_14_out, not_1_out, not_2_out, not_3_out,
       not_4_out, not_5_out, not_6_out, not_7_out, not_8_out, not_9_out, not_10_out, not_11_out;

  not not_1 (not_1_out, Q3);
  not not_2 (not_2_out, Q2);
  not not_3 (not_3_out, Q1);
  not not_4 (not_4_out, Q0);
  and and_1 (and_1_out, Q2, Q0);
  and and_2 (and_2_out, Q2, Q1);
  not not_5 (not_5_out, Q1);
  and and_3 (and_3_out, Q3, not_5_out, not_6_out);
  not not_6 (not_6_out, Q0);
  and and_4 (and_4_out, Q3, Q1, Q0);
  and and_5 (and_5_out, Q1, Q0);
  not not_7 (not_7_out, Q1);
  and and_6 (and_6_out, Q2, not_7_out, not_8_out);
  not not_8 (not_8_out, Q0);
  not not_9 (not_9_out, Q1);
  and and_7 (and_7_out, Q3, not_9_out, not_10_out);
  not not_10 (not_10_out, Q0);
  and and_8 (and_8_out, Q3, Q2);
  not not_11 (not_11_out, Q0);
  and and_9 (and_9_out, Q3, Q1);
  and and_10 (and_10_out, Q3, Q2);
  and and_11 (and_11_out, not_1_out, not_2_out, not_3_out, not_4_out);
  and and_12 (and_12_out, Q3, Q0);
  and and_13 (and_13_out, Q3, Q1);
  and and_14 (and_14_out, Q3, Q2);
  or or_1 (S2, and_1_out, and_2_out, and_3_out, and_4_out);
  or or_2 (S1, and_5_out, and_6_out, and_7_out, and_8_out);
  or or_3 (S0, not_11_out, and_9_out, and_10_out);
  or or_4 (S3, and_11_out, and_12_out, and_13_out, and_14_out);
endmodule

module \xor  (
  input  in_1,
  input  in_2,
  output out_3
);

  wire and_1_out, and_2_out, not_1_out, not_2_out;

  not not_1 (not_1_out, in_1);
  not not_2 (not_2_out, in_2);
  and and_1 (and_1_out, not_1_out, in_2);
  or or_1 (out_3, and_1_out, and_2_out);
  and and_2 (and_2_out, in_1, not_2_out);
endmodule

module \xnor  (
  input  in_1,
  input  in_2,
  output out_3
);

  wire xor_1_out_3;

  \xor  xor_1 (.in_1(in_1), .in_2(in_2), .out_3(xor_1_out_3));
  not not_1 (out_3, xor_1_out_3);
endmodule

module comparador_de_magnitude (
  input  [3:0] X,
  input  [3:0] bota_um_rotulo,
  output out_3,
  output X_ALE,
  output X_ALE_2
);

  wire and_1_out, and_2_out, and_3_out, and_4_out, and_5_out, and_7_out, xnor_1_out_3, xnor_2_out_3,
       xnor_3_out_3, xnor_4_out_3;

  \xnor  xnor_1 (.in_1(X[3]), .in_2(bota_um_rotulo[3]), .out_3(xnor_1_out_3));
  and and_1 (and_1_out, xnor_1_out_3, xnor_2_out_3);
  \xnor  xnor_2 (.in_1(X[2]), .in_2(bota_um_rotulo[2]), .out_3(xnor_2_out_3));
  \xnor  xnor_3 (.in_1(X[1]), .in_2(bota_um_rotulo[1]), .out_3(xnor_3_out_3));
  \xnor  xnor_4 (.in_1(X[0]), .in_2(bota_um_rotulo[0]), .out_3(xnor_4_out_3));
  and and_2 (and_2_out, ~bota_um_rotulo[0], X[0], xnor_3_out_3, xnor_2_out_3, xnor_1_out_3);  // AND_Gate
  and and_3 (and_3_out, ~bota_um_rotulo[1], X[1], xnor_2_out_3, xnor_1_out_3);  // AND_Gate
  and and_4 (and_4_out, ~bota_um_rotulo[2], X[2], xnor_1_out_3);  // AND_Gate
  and and_5 (and_5_out, ~X[2], X[3]);  // AND_Gate
  and and_6 (out_3, and_1_out, and_7_out);
  and and_7 (and_7_out, xnor_3_out_3, xnor_4_out_3);
  or or_1 (X_ALE_2, and_2_out, and_3_out, and_4_out, and_5_out);
  \xnor  xnor_5 (.in_1(out_3), .in_2(X_ALE_2), .out_3(X_ALE));

  // Notes on the sheet:
  //   A
  //   B
endmodule

module core_akina_hills_v8_nitro (
  input  CONFIRMAR,
  input  swap_y_a,
  input  gerar,
  input  [3:0] a,
  input  confirmar_a,
  input  reset_placar,
  input  swap_y__b,
  input  [3:0] b,
  input  stop_a,
  input  confirmar_b,
  input  change_players,
  input  stop_b,
  output maior,
  output igual,
  output menor,
  output [3:0] placary,
  output [3:0] placarx,
  output [3:0] current_xa,
  output [3:0] current_ya,
  output stop_a_f,
  output [3:0] current_yb,
  output stop_b_f,
  output [3:0] current_xb
);

  wire and_1_out, and_2_out, d_ff_1_qn, d_ff_2_qn, d_ff_3_qn, not_1_out, not_2_out, not_3_out;
  wire [4:0] modurimasen_1_soma, modurimasen_2_soma, multiplexer_1_out, somador_1_out_3;
  wire [7:0] random_1_out;

  not not_1 (not_1_out, stop_a);
  not not_2 (not_2_out, stop_b);
  D_Flip_Flop d_ff_1 (.clk(not_1_out), .D(d_ff_1_qn), .Q(stop_a_f), .Qn(d_ff_1_qn));  // open: preset, en, reset
  D_Flip_Flop d_ff_2 (.clk(not_2_out), .D(d_ff_2_qn), .Q(stop_b_f), .Qn(d_ff_2_qn));  // open: preset, en, reset
  modurimasen modurimasen_1 (
    .ada(swap_y__b), .\input (b), .confirmar(confirmar_b), .soma(modurimasen_1_soma), .current_y(current_yb),
    .current_x(current_xb));
  modurimasen modurimasen_2 (
    .ada(swap_y_a), .\input (a), .confirmar(confirmar_a), .soma(modurimasen_2_soma), .current_y(current_ya),
    .current_x(current_xa));
  Random random_1 (.clk(gerar), .out(random_1_out));  // open: next, clr
  Multiplexer #(.width(5)) multiplexer_1 (
    .in0(modurimasen_2_soma), .in1(modurimasen_1_soma), .out(multiplexer_1_out), .sel(change_players),
    .en(not_3_out));
  somador somador_1 (.in_1(random_1_out[3:0]), .in_2(random_1_out[7:4]), .out_3(somador_1_out_3));
  D_Flip_Flop d_ff_3 (.clk(CONFIRMAR), .D(d_ff_3_qn), .Qn(d_ff_3_qn));  // open: Q, preset, en, reset
  not not_3 (not_3_out, d_ff_3_qn);
  Comparator #(.width(5)) comparator_1 (.a(somador_1_out_3), .b(multiplexer_1_out), .gt(maior), .eq(igual), .lt(menor));
  and and_1 (and_1_out, ~change_players, igual);  // AND_Gate
  and and_2 (and_2_out, change_players, igual);
  placar placar_1 (.placar_reset(reset_placar), .count(and_1_out), .TUS(placary));
  placar placar_2 (.placar_reset(reset_placar), .count(and_2_out), .TUS(placarx));
endmodule

module guil (
  input  dm,
  input  um,
  input  ds,
  input  us,
  output c,
  output b,
  output a
);

  and and_1 (c, um, ds, us);
  and and_2 (b, ds, us);

  assign a = us;
endmodule

module mintira (
  input  [3:0] entrada,
  output sinal,
  output [3:0] saida
);

  wire and_2_out, and_3_out, and_4_out, and_5_out, and_6_out, and_7_out, and_8_out, not_1_out, not_2_out,
       not_3_out, not_4_out, not_5_out, not_6_out, not_7_out, not_8_out, not_9_out, not_10_out, not_11_out;

  not not_1 (not_1_out, entrada[2]);
  not not_2 (not_2_out, entrada[1]);
  not not_3 (not_3_out, entrada[0]);
  not not_4 (not_4_out, entrada[3]);
  not not_5 (not_5_out, entrada[1]);
  not not_6 (not_6_out, entrada[0]);
  not not_7 (not_7_out, entrada[2]);
  not not_8 (not_8_out, entrada[2]);
  not not_9 (not_9_out, entrada[3]);
  not not_10 (not_10_out, entrada[0]);
  not not_11 (not_11_out, entrada[1]);
  and and_1 (saida[3], entrada[3], not_1_out, not_2_out, not_3_out);
  and and_2 (and_2_out, not_4_out, entrada[2]);
  and and_3 (and_3_out, entrada[2], not_5_out, not_6_out);
  and and_4 (and_4_out, entrada[3], not_7_out, entrada[0]);
  and and_5 (and_5_out, entrada[3], not_8_out, entrada[1]);
  and and_6 (and_6_out, not_9_out, entrada[1]);
  and and_7 (and_7_out, entrada[1], not_10_out);
  and and_8 (and_8_out, entrada[3], not_11_out, entrada[0]);
  or or_1 (saida[2], and_2_out, and_3_out, and_4_out, and_5_out);
  or or_2 (saida[1], and_6_out, and_7_out, and_8_out);

  assign saida[0] = entrada[0];
  assign sinal = entrada[3];
endmodule

module somador (
  input  [3:0] in_1,
  input  [3:0] in_2,
  output [4:0] out_3
);

  wire mintira_1_sinal, mintira_2_sinal;
  wire [3:0] mintira_1_saida, mintira_2_saida;
  wire [4:0] bit_extender_1_out, bit_extender_2_out;

  LED led_1 (.in(mintira_1_sinal));
  LED led_2 (.in(mintira_2_sinal));
  Hex_Digit_Display hex_digit_display_1 (.value(mintira_1_saida));  // open: dp
  mintira mintira_1 (.saida(mintira_1_saida), .entrada(in_1), .sinal(mintira_1_sinal));
  assign bit_extender_1_out = {{1{in_1[3]}}, in_1};  // Bit_Extender bit_extender_1
  Hex_Digit_Display hex_digit_display_2 (.value(mintira_2_saida));  // open: dp
  mintira mintira_2 (.saida(mintira_2_saida), .entrada(in_2), .sinal(mintira_2_sinal));
  assign bit_extender_2_out = {{1{in_2[3]}}, in_2};  // Bit_Extender bit_extender_2
  Adder #(.width(5)) adder_1 (.a(bit_extender_2_out), .b(bit_extender_1_out), .out(out_3));  // open: cin, cout
  Hex_Digit_Display hex_digit_display_3 ();  // open: value, dp
endmodule

module placar (
  input  placar_reset,
  input  count,
  output [3:0] TUS
);

  wire cont_placar_1_d2, cont_placar_1_f, cont_placar_1_g, cont_placar_1_s;
  wire [3:0] undriven;

  D_Flip_Flop d_ff_1 (.clk(count), .D(cont_placar_1_d2), .Q(TUS[2]), .preset(undriven[2]));  // open: Qn, en, reset
  D_Flip_Flop d_ff_2 (
    .clk(count), .D(cont_placar_1_s), .Q(TUS[3]), .preset(undriven[3]), .reset(placar_reset));  // open: Qn, en
  D_Flip_Flop d_ff_3 (
    .clk(count), .D(cont_placar_1_f), .Q(TUS[1]), .preset(undriven[1]), .reset(placar_reset));  // open: Qn, en
  D_Flip_Flop d_ff_4 (
    .clk(count), .D(cont_placar_1_g), .Q(TUS[0]), .preset(undriven[0]), .reset(placar_reset));  // open: Qn, en
  cont_placar cont_placar_1 (
    .a(TUS[3]), .b(TUS[2]), .c(TUS[1]), .d(TUS[0]), .s(cont_placar_1_s), .d2(cont_placar_1_d2),
    .f(cont_placar_1_f), .g(cont_placar_1_g));
  Hex_Digit_Display hex_digit_display_1 (.value(TUS));  // open: dp
endmodule

module cont_placar (
  input  a,
  input  b,
  input  c,
  input  d,
  output s,
  output d2,
  output f,
  output g
);

  wire and_1_out, and_2_out, and_3_out, and_4_out, and_5_out, and_6_out, and_7_out, and_8_out, and_9_out,
       and_10_out, not_1_out, not_2_out, not_3_out, not_4_out, not_5_out, not_6_out, not_7_out, not_8_out,
       not_9_out, not_10_out, not_11_out, not_12_out;

  not not_1 (not_1_out, a);
  not not_2 (not_2_out, b);
  not not_3 (not_3_out, c);
  not not_4 (not_4_out, d);
  not not_5 (not_5_out, b);
  and and_1 (and_1_out, not_5_out, c, d);
  and and_2 (and_2_out, b, not_6_out);
  not not_6 (not_6_out, c);
  and and_3 (and_3_out, b, not_7_out);
  not not_7 (not_7_out, d);
  not not_8 (not_8_out, c);
  and and_4 (and_4_out, not_8_out, d);
  not not_9 (not_9_out, a);
  and and_5 (and_5_out, not_9_out, c, not_10_out);
  not not_10 (not_10_out, d);
  not not_11 (not_11_out, b);
  and and_6 (and_6_out, not_11_out, c, not_12_out);
  not not_12 (not_12_out, d);
  not not_13 (g, d);
  and and_7 (and_7_out, not_1_out, b, c, d);
  and and_8 (and_8_out, a, not_2_out);
  and and_9 (and_9_out, a, not_3_out);
  and and_10 (and_10_out, a, not_4_out);
  or or_1 (d2, and_1_out, and_2_out, and_3_out);
  or or_2 (f, and_4_out, and_5_out, and_6_out);
  or or_3 (s, and_7_out, and_8_out, and_9_out, and_10_out);
endmodule

module modurimasen (
  input  ada,
  input  [3:0] \input ,
  input  confirmar,
  output [4:0] soma,
  output [3:0] current_y,
  output [3:0] current_x
);

  wire d_ff_1_qn, undriven_2;
  wire [3:0] undriven;

  Multiplexer #(.width(4), .enable("false")) multiplexer_1 (
    .in0(\input ), .in1(undriven), .out(current_y), .sel(d_ff_1_qn));
  D_Flip_Flop d_ff_1 (.clk(confirmar), .D(d_ff_1_qn), .Qn(d_ff_1_qn));  // open: Q, preset, en, reset
  D_Flip_Flop d_ff_2 (.clk(ada), .D(current_y[0]), .Q(current_x[0]), .reset(undriven_2));  // open: Qn, preset, en
  D_Flip_Flop d_ff_3 (.clk(ada), .D(current_y[1]), .Q(current_x[1]), .reset(undriven_2));  // open: Qn, preset, en
  somador somador_1 (.in_1(current_y), .in_2(current_x), .out_3(soma));
  D_Flip_Flop d_ff_4 (.clk(ada), .D(current_y[2]), .Q(current_x[2]), .reset(undriven_2));  // open: Qn, preset, en
  D_Flip_Flop d_ff_5 (.clk(ada), .D(current_y[3]), .Q(current_x[3]), .reset(undriven_2));  // open: Qn, preset, en
endmodule
