// Logisim project projeto_2.3.circ as structural Verilog: 7 circuits, main circuit main
module main (
  input  in_1,
  input  in_2,
  input  in_3
);

  wire contador_9_ao_0_1_out_5;
  wire [3:0] contador_9_ao_0_1_out_4, contador_de_5_a_0_1_out_4;

  Hex_Digit_Display hex_digit_display_1 (.value(contador_de_5_a_0_1_out_4));  // open: dp
  contador_9_ao_0 contador_9_ao_0_1 (
    .in_1(in_1), .reset(in_2), .in_3(in_3), .out_4(contador_9_ao_0_1_out_4), .out_5(contador_9_ao_0_1_out_5));
  Hex_Digit_Display hex_digit_display_2 (.value(contador_9_ao_0_1_out_4));  // open: dp
  contador_de_5_a_0 contador_de_5_a_0_1 (
    .in_1(contador_9_ao_0_1_out_5), .reset(in_2), .in_3(in_3), .out_4(contador_de_5_a_0_1_out_4));
endmodule

module contador_5 (
  input  Q3,
  input  Q2,
  input  Q1,
  input  Q0,
  output S3,
  output S2,
  output S1,
  output S0
);

  wire and_1_out, and_2_out, and_3_out, and_4_out, not_1_out, not_2_out, not_3_out, not_4_out, not_5_out;

  not not_1 (not_1_out, Q2);
  not not_2 (not_2_out, Q1);
  and and_1 (and_1_out, not_1_out, not_2_out, not_3_out);
  not not_3 (not_3_out, Q0);
  and and_2 (and_2_out, Q2, Q0);
  and and_3 (and_3_out, Q1, Q0);
  and and_4 (and_4_out, Q2, not_4_out);
  not not_4 (not_4_out, Q0);
  not not_5 (not_5_out, Q0);
  or or_1 (S0, not_5_out, Q3);
  or or_2 (S2, and_1_out, and_2_out);
  or or_3 (S1, and_3_out, and_4_out);

  assign S3 = Q3;
endmodule

module contador_9_ao_0 (
  input  in_1,
  input  reset,
  input  in_3,
  output [3:0] out_4,
  output out_5
);

  wire comparator_1_eq, contador_1_s0, contador_1_s1, contador_1_s2, contador_1_s3, not_1_out;

  D_Flip_Flop d_ff_1 (.clk(in_1), .D(contador_1_s3), .Q(out_4[3]), .en(not_1_out), .reset(reset));  // open: Qn, preset
  not not_1 (not_1_out, in_3);
  D_Flip_Flop d_ff_2 (.clk(in_1), .D(contador_1_s2), .Q(out_4[2]), .en(not_1_out), .reset(reset));  // open: Qn, preset
  D_Flip_Flop d_ff_3 (.clk(in_1), .D(contador_1_s1), .Q(out_4[1]), .en(not_1_out), .reset(reset));  // open: Qn, preset
  D_Flip_Flop d_ff_4 (.clk(in_1), .D(contador_1_s0), .Q(out_4[0]), .en(not_1_out), .reset(reset));  // open: Qn, preset
  contador contador_1 (
    .Q3(out_4[3]), .Q2(out_4[2]), .Q1(out_4[1]), .Q0(out_4[0]), .S3(contador_1_s3), .S2(contador_1_s2),
    .S1(contador_1_s1), .S0(contador_1_s0));
  Comparator #(.width(4)) comparator_1 (.a(out_4), .b(4'b0000), .eq(comparator_1_eq));  // open: gt, lt
  not not_2 (out_5, comparator_1_eq);
endmodule

module contador (
  input  Q3,
  input  Q2,
  input  Q1,
  input  Q0,
  output S3,
  output S2,
  output S1,
  output S0
);

  wire and_1_out, and_2_out, and_3_out, and_4_out, and_5_out, and_6_out, and_7_out, and_8_out, and_9_out,
       and_10_out, and_11_out, and_12_out, and_13_out, not_1_out, not_2_out, not_3_out, not_4_out, not_5_out,
       not_6_out, not_7_out, not_8_out, not_9_out;

  not not_1 (not_1_out, Q3);
  not not_2 (not_2_out, Q2);
  not not_3 (not_3_out, Q1);
  not not_4 (not_4_out, Q0);
  and and_1 (and_1_out, Q2, Q0);
  and and_2 (and_2_out, Q2, Q1);
  and and_3 (and_3_out, Q3, not_5_out);
  not not_5 (not_5_out, Q0);
  and and_4 (and_4_out, Q3, Q1);
  and and_5 (and_5_out, Q1, Q0);
  and and_6 (and_6_out, Q2, not_6_out, not_7_out);
  not not_6 (not_6_out, Q1);
  not not_7 (not_7_out, Q0);
  and and_7 (and_7_out, Q3, not_8_out);
  not not_8 (not_8_out, Q0);
  and and_8 (and_8_out, Q3, Q2);
  not not_9 (not_9_out, Q0);
  and and_9 (and_9_out, Q3, Q1);
  and and_10 (and_10_out, Q3, Q2);
  and and_11 (and_11_out, not_1_out, not_2_out, not_3_out, not_4_out);
  or or_1 (S3, and_11_out, and_12_out, and_13_out);
  and and_12 (and_12_out, Q3, Q0);
  and and_13 (and_13_out, Q3, Q1);
  or or_2 (S2, and_1_out, and_2_out, and_3_out, and_4_out);
  or or_3 (S1, and_5_out, and_6_out, and_7_out, and_8_out);
  or or_4 (S0, not_9_out, and_9_out, and_10_out);
endmodule

module contador_de_5_a_0 (
  input  in_1,
  input  reset,
  input  in_3,
  output [3:0] out_4
);

  wire contador_5_1_s0, contador_5_1_s1, contador_5_1_s2, contador_5_1_s3, not_1_out;

  D_Flip_Flop d_ff_1 (
    .clk(in_1), .D(contador_5_1_s3), .Q(out_4[3]), .en(not_1_out), .reset(reset));  // open: Qn, preset
  not not_1 (not_1_out, in_3);
  D_Flip_Flop d_ff_2 (
    .clk(in_1), .D(contador_5_1_s2), .Q(out_4[2]), .en(not_1_out), .reset(reset));  // open: Qn, preset
  D_Flip_Flop d_ff_3 (
    .clk(in_1), .D(contador_5_1_s1), .Q(out_4[1]), .en(not_1_out), .reset(reset));  // open: Qn, preset
  D_Flip_Flop d_ff_4 (
    .clk(in_1), .D(contador_5_1_s0), .Q(out_4[0]), .en(not_1_out), .reset(reset));  // open: Qn, preset
  contador_5 contador_5_1 (
    .Q3(out_4[3]), .Q2(out_4[2]), .Q1(out_4[1]), .Q0(out_4[0]), .S3(contador_5_1_s3), .S2(contador_5_1_s2),
    .S1(contador_5_1_s1), .S0(contador_5_1_s0));
endmodule

module contador_1 (
  input  Q3,
  input  Q2,
  input  Q1,
  input  Q0,
  output S3,
  output S2,
  output S1,
  output S0
);

  wire not_1_out;

  not not_1 (not_1_out, Q0);
  or or_1 (S0, not_1_out, Q2);

  assign S1 = Q2;
  assign S2 = Q2;
  assign S3 = Q2;
endmodule

module contador_1_a_0 (
  input  reset,
  input  in_2
);

  wire contador_1_1_s0, contador_1_1_s1, contador_1_1_s2, contador_1_1_s3, not_1_out, undriven;
  wire [3:0] d_ff_4_q;

  not not_1 (not_1_out, in_2);
  D_Flip_Flop d_ff_1 (
    .clk(undriven), .D(contador_1_1_s3), .Q(d_ff_4_q[3]), .en(not_1_out), .reset(reset));  // open: Qn, preset
  D_Flip_Flop d_ff_2 (
    .clk(undriven), .D(contador_1_1_s2), .Q(d_ff_4_q[2]), .en(not_1_out), .reset(reset));  // open: Qn, preset
  D_Flip_Flop d_ff_3 (
    .clk(undriven), .D(contador_1_1_s1), .Q(d_ff_4_q[1]), .en(not_1_out), .reset(reset));  // open: Qn, preset
  D_Flip_Flop d_ff_4 (
    .clk(undriven), .D(contador_1_1_s0), .Q(d_ff_4_q[0]), .en(not_1_out), .reset(reset));  // open: Qn, preset
  contador_1 contador_1_1 (
    .Q3(d_ff_4_q[3]), .Q2(d_ff_4_q[2]), .Q1(d_ff_4_q[1]), .Q0(d_ff_4_q[0]), .S3(contador_1_1_s3),
    .S2(contador_1_1_s2), .S1(contador_1_1_s1), .S0(contador_1_1_s0));
  Hex_Digit_Display hex_digit_display_1 (.value(d_ff_4_q));  // open: dp
endmodule
