// Logisim project projeto-2.37.circ as structural Verilog: 14 circuits, main circuit main
module main (
  input  [3:0] in_1,
  input  in_2,
  input  [3:0] in_3,
  input  [3:0] in_4,
  input  [3:0] in_5,
  input  [3:0] in_6,
  input  [3:0] in_7,
  input  in_8,
  input  in_9,
  input  in_10
);

  wire A_DEAD, B_DEAD, CHUTAR, clk, \começar , CONFIRMAR, EMPATE, GERAR, IGUAL, JOGADOR_A_VENCEU,
       JOGADOR_B_VENCEU, MAIOR, MENOR, RESET, Reset_Placar, STOP, STOPA, STOPB, tunnel;
  wire [3:0] current_xa, current_xb, current_ya, current_yb, DMA, DMB, DSA, DSB, placar_a, placar_b, UMA,
       UMB, USA, USB;

  Hex_Digit_Display hex_digit_display_1 (.value(DMA));  // open: dp
  Hex_Digit_Display hex_digit_display_2 (.value(UMA));  // open: dp
  Hex_Digit_Display hex_digit_display_3 (.value(current_xa));  // open: dp
  timer timer_1 (
    .RESET(RESET), .CLK(clk), .TDM(DMB), .UM(in_3), .TUM(UMB), .DS(in_4), .TDS(DSB), .x(in_5), .TUS(USB),
    .SELEC(in_2), .DM(in_1), .stop(STOPB), .over(A_DEAD));
  timer timer_2 (
    .RESET(RESET), .CLK(clk), .TDM(DMA), .UM(in_3), .TUM(UMA), .DS(in_4), .TDS(DSA), .x(in_5), .TUS(USA),
    .SELEC(in_2), .DM(in_1), .stop(STOPA), .over(B_DEAD));
  LED led_1 ();  // open: in
  LED led_2 ();  // open: in
  LED led_3 (.in(JOGADOR_A_VENCEU));
  Hex_Digit_Display hex_digit_display_4 (.value(DSA));  // open: dp
  Hex_Digit_Display hex_digit_display_5 (.value(USA));  // open: dp
  LED led_4 (.in(B_DEAD));
  Hex_Digit_Display hex_digit_display_6 (.value(current_ya));  // open: dp
  Button button_1 (.out(GERAR));
  LED led_5 (.in(tunnel));
  LED led_6 (.in(MENOR));
  Hex_Digit_Display hex_digit_display_7 (.value(placar_a));  // open: dp
  Clock clock_1 (.out(clk));
  Button button_2 (.out(\começar ));
  Button button_3 (.out(CHUTAR));
  LED led_7 (.in(tunnel));
  LED led_8 (.in(MAIOR));
  LED led_9 (.in(IGUAL));
  LED led_10 (.in(EMPATE));
  Hex_Digit_Display hex_digit_display_8 (.value(placar_b));  // open: dp
  Button button_4 (.out(Reset_Placar));
  Button button_5 (.out(RESET));
  core_v8_nitro core_v8_nitro_1 (
    .gerar(GERAR), .a(in_6), .current_xa(current_xa), .swap_y__b(in_10), .current_ya(current_ya), .b(in_7),
    .current_yb(current_yb), .CONFIRMAR(CONFIRMAR), .placar_a(placar_a), .placar_b(placar_b),
    .current_xb(current_xb), .reset_placar(Reset_Placar), .confirmar_b(CHUTAR), .confirmar_a(CHUTAR),
    .change_players(in_8), .maior(MAIOR), .igual(IGUAL), .menor(MENOR), .swap_a(in_9), .led(tunnel),
    .jogador_a_venceu(JOGADOR_A_VENCEU), .jogador_b_venceu(JOGADOR_B_VENCEU), .empate(EMPATE),
    .stop_a_f(STOPB), .stop_b_f(STOPA), .\começar (\começar ), .stop(STOP));
  Hex_Digit_Display hex_digit_display_9 (.value(UMB));  // open: dp
  Hex_Digit_Display hex_digit_display_10 (.value(DMB));  // open: dp
  Button button_6 (.out(CONFIRMAR));
  LED led_11 ();  // open: in
  LED led_12 ();  // open: in
  Button button_7 (.out(STOP));
  LED led_13 (.in(JOGADOR_B_VENCEU));
  Hex_Digit_Display hex_digit_display_11 (.value(current_xb));  // open: dp
  Hex_Digit_Display hex_digit_display_12 (.value(DSB));  // open: dp
  Hex_Digit_Display hex_digit_display_13 (.value(USB));  // open: dp
  LED led_14 (.in(A_DEAD));
  Hex_Digit_Display hex_digit_display_14 (.value(current_yb));  // open: dp

  // Other names for the same wires on the sheet: ALTERNAR_O_JOGADOR = in_8; dm[3:0] = in_1; ds[3:0] = in_4;
  //   JOGADA_A[3:0] = in_6; JOGADA_B[3:0] = in_7; SELECT = in_2; swap_a = in_9; swap_b = in_10; um[3:0] = in_3;
  //   us[3:0] = in_5

  // Notes on the sheet:
  //   in_3: pull=up
endmodule

// Timer
module timer (
  input  RESET,
  input  [3:0] DM,
  input  [3:0] UM,
  input  [3:0] DS,
  input  [3:0] x,
  input  CLK,
  input  stop,
  input  SELEC,
  output [3:0] TDM,
  output [3:0] TUM,
  output over,
  output [3:0] TDS,
  output [3:0] TUS
);

  wire a, and_1_out, and_2_out, and_7_out, b, c, comparator_1_eq, comparator_2_eq, comparator_3_eq,
       cont_d_1_s0, cont_d_1_s1, cont_d_1_s2, cont_d_1_s3, cont_d_2_s0, cont_d_2_s1, cont_d_2_s2,
       cont_d_2_s3, cont_u_1_s0, cont_u_1_s1, cont_u_1_s2, cont_u_1_s3, cont_u_2_s0, cont_u_2_s1,
       cont_u_2_s2, cont_u_2_s3, guil_1_a, guil_1_b, guil_1_c, multiplexer_5_out, not_1_out, or_1_out;
  wire [3:0] multiplexer_1_out, multiplexer_2_out, multiplexer_3_out, multiplexer_4_out;

  Multiplexer #(.width(4), .enable("false")) multiplexer_1 (
    .in0(DM), .out(multiplexer_1_out), .sel(SELEC));  // open: in1
  D_Flip_Flop d_ff_1 (
    .clk(b), .D(cont_u_1_s3), .Q(TUM[3]), .preset(multiplexer_2_out[3]), .en(not_1_out), .reset(RESET));  // open: Qn
  Multiplexer #(.width(4), .enable("false")) multiplexer_2 (
    .in0(UM), .out(multiplexer_2_out), .sel(SELEC));  // open: in1
  D_Flip_Flop d_ff_2 (
    .clk(a), .D(cont_d_2_s3), .Q(TDS[3]), .preset(multiplexer_3_out[3]), .en(not_1_out), .reset(RESET));  // open: Qn
  Multiplexer #(.width(4), .enable("false")) multiplexer_3 (
    .in0(DS), .out(multiplexer_3_out), .sel(SELEC));  // open: in1
  Multiplexer #(.width(4), .enable("false")) multiplexer_4 (
    .in0(x), .out(multiplexer_4_out), .sel(SELEC));  // open: in1
  D_Flip_Flop d_ff_3 (
    .clk(c), .D(cont_d_1_s2), .Q(TDM[2]), .preset(multiplexer_1_out[2]), .en(not_1_out), .reset(RESET));  // open: Qn
  D_Flip_Flop d_ff_4 (
    .clk(c), .D(cont_d_1_s3), .Q(TDM[3]), .preset(multiplexer_1_out[3]), .en(not_1_out), .reset(RESET));  // open: Qn
  D_Flip_Flop d_ff_5 (
    .clk(b), .D(cont_u_1_s2), .Q(TUM[2]), .preset(multiplexer_2_out[2]), .en(not_1_out), .reset(RESET));  // open: Qn
  D_Flip_Flop d_ff_6 (
    .clk(a), .D(cont_d_2_s2), .Q(TDS[2]), .preset(multiplexer_3_out[2]), .en(not_1_out), .reset(RESET));  // open: Qn
  D_Flip_Flop d_ff_7 (
    .clk(multiplexer_5_out), .D(cont_u_2_s2), .Q(TUS[2]), .preset(multiplexer_4_out[2]), .en(not_1_out),
    .reset(RESET));  // open: Qn
  D_Flip_Flop d_ff_8 (
    .clk(multiplexer_5_out), .D(cont_u_2_s3), .Q(TUS[3]), .preset(multiplexer_4_out[3]), .en(not_1_out),
    .reset(RESET));  // open: Qn
  D_Flip_Flop d_ff_9 (
    .clk(c), .D(cont_d_1_s1), .Q(TDM[1]), .preset(multiplexer_1_out[1]), .en(not_1_out), .reset(RESET));  // open: Qn
  D_Flip_Flop d_ff_10 (
    .clk(b), .D(cont_u_1_s1), .Q(TUM[1]), .preset(multiplexer_2_out[1]), .en(not_1_out), .reset(RESET));  // open: Qn
  D_Flip_Flop d_ff_11 (
    .clk(a), .D(cont_d_2_s1), .Q(TDS[1]), .preset(multiplexer_3_out[1]), .en(not_1_out), .reset(RESET));  // open: Qn
  D_Flip_Flop d_ff_12 (
    .clk(multiplexer_5_out), .D(cont_u_2_s1), .Q(TUS[1]), .preset(multiplexer_4_out[1]), .en(not_1_out),
    .reset(RESET));  // open: Qn
  D_Flip_Flop d_ff_13 (
    .clk(c), .D(cont_d_1_s0), .Q(TDM[0]), .preset(multiplexer_1_out[0]), .en(not_1_out), .reset(RESET));  // open: Qn
  cont_d cont_d_1 (
    .Q3(TDM[3]), .Q2(TDM[2]), .Q1(TDM[1]), .Q0(TDM[0]), .S3(cont_d_1_s3), .S2(cont_d_1_s2), .S1(cont_d_1_s1),
    .S0(cont_d_1_s0));
  D_Flip_Flop d_ff_14 (
    .clk(b), .D(cont_u_1_s0), .Q(TUM[0]), .preset(multiplexer_2_out[0]), .en(not_1_out), .reset(RESET));  // open: Qn
  cont_u cont_u_1 (
    .Q3(TUM[3]), .Q2(TUM[2]), .Q1(TUM[1]), .Q0(TUM[0]), .S3(cont_u_1_s3), .S2(cont_u_1_s2), .S1(cont_u_1_s1),
    .S0(cont_u_1_s0));
  D_Flip_Flop d_ff_15 (
    .clk(a), .D(cont_d_2_s0), .Q(TDS[0]), .preset(multiplexer_3_out[0]), .en(not_1_out), .reset(RESET));  // open: Qn
  cont_d cont_d_2 (
    .Q3(TDS[3]), .Q2(TDS[2]), .Q1(TDS[1]), .Q0(TDS[0]), .S3(cont_d_2_s3), .S2(cont_d_2_s2), .S1(cont_d_2_s1),
    .S0(cont_d_2_s0));
  D_Flip_Flop d_ff_16 (
    .clk(multiplexer_5_out), .D(cont_u_2_s0), .Q(TUS[0]), .preset(multiplexer_4_out[0]), .en(not_1_out),
    .reset(RESET));  // open: Qn
  cont_u cont_u_2 (
    .Q3(TUS[3]), .Q2(TUS[2]), .Q1(TUS[1]), .Q0(TUS[0]), .S3(cont_u_2_s3), .S2(cont_u_2_s2), .S1(cont_u_2_s1),
    .S0(cont_u_2_s0));
  Hex_Digit_Display hex_digit_display_1 (.value(TDM));  // open: dp
  Hex_Digit_Display hex_digit_display_2 (.value(TUM));  // open: dp
  Hex_Digit_Display hex_digit_display_3 (.value(TDS));  // open: dp
  Hex_Digit_Display hex_digit_display_4 (.value(TUS));  // open: dp
  and and_1 (and_1_out, ~TDM[0], ~TDM[1], ~TDM[2], ~TDM[3]);  // AND_Gate
  Comparator #(.width(4)) comparator_1 (.a(TUM), .b(4'b0000), .eq(comparator_1_eq));  // open: gt, lt
  Comparator #(.width(4)) comparator_2 (.a(TDS), .b(4'b0000), .eq(comparator_2_eq));  // open: gt, lt
  Multiplexer #(.enable("false")) multiplexer_5 (.in0(CLK), .out(multiplexer_5_out), .sel(1'b0));  // open: in1
  not not_1 (not_1_out, or_1_out);
  or or_1 (or_1_out, stop, over);
  Comparator #(.width(4)) comparator_3 (.a(TUS), .b(4'b0000), .eq(comparator_3_eq));  // open: gt, lt
  and and_2 (and_2_out, ~comparator_2_eq, comparator_3_eq);  // AND_Gate
  guil guil_1 (
    .dm(and_1_out), .um(comparator_1_eq), .ds(comparator_2_eq), .us(comparator_3_eq), .c(guil_1_c),
    .b(guil_1_b), .a(guil_1_a));
  and and_3 (over, and_1_out, comparator_1_eq, comparator_2_eq, comparator_3_eq);
  and and_4 (a, and_7_out, ~and_2_out);  // AND_Gate
  and and_5 (c, SELEC, CLK, guil_1_c);
  and and_6 (b, SELEC, CLK, guil_1_b);
  and and_7 (and_7_out, SELEC, CLK, guil_1_a);

  // Other names for the same wires on the sheet: ada = SELEC; f = CLK

  // Notes on the sheet:
  //   DEZENA DE MINUTOS
  //   UNIDADE DE MINUTOS
  //   DEZENA DE SEGUNDOS
  //   UNIDADE DE MINUTOS
endmodule

module cont_d (
  input  Q3,
  input  Q2,
  input  Q1,
  input  Q0,
  output S3,
  output S2,
  output S1,
  output S0
);

  wire and_1_out, and_2_out, and_3_out, and_4_out, and_5_out, and_6_out, and_7_out, and_8_out, and_9_out,
       and_10_out, not_1_out, not_2_out, not_3_out, not_4_out, not_5_out, not_6_out, not_7_out, not_8_out,
       not_9_out, not_10_out;

  and and_1 (and_1_out, Q2, Q1, Q0);
  not not_1 (not_1_out, Q2);
  not not_2 (not_2_out, Q1);
  not not_3 (not_3_out, Q0);
  not not_4 (not_4_out, Q3);
  not not_5 (not_5_out, Q3);
  not not_6 (not_6_out, Q1);
  not not_7 (not_7_out, Q0);
  not not_8 (not_8_out, Q0);
  not not_9 (not_9_out, Q0);
  not not_10 (not_10_out, Q0);
  or or_1 (S3, and_1_out, Q3);
  and and_2 (and_2_out, not_1_out, not_2_out, not_3_out);
  and and_3 (and_3_out, Q2, Q0);
  and and_4 (and_4_out, not_4_out, Q2, Q1);
  and and_5 (and_5_out, not_5_out, not_6_out, not_7_out);
  and and_6 (and_6_out, Q1, Q0);
  and and_7 (and_7_out, Q3, Q2, not_8_out);
  and and_8 (and_8_out, Q1, not_9_out);
  and and_9 (and_9_out, Q2, not_10_out);
  and and_10 (and_10_out, Q2, Q1);
  or or_2 (S2, and_2_out, and_3_out, and_4_out);
  or or_3 (S1, and_5_out, and_6_out, and_7_out);
  or or_4 (S0, and_8_out, and_9_out, and_10_out, Q3);
endmodule

module cont_u (
  input  Q3,
  input  Q2,
  input  Q1,
  input  Q0,
  output S3,
  output S2,
  output S1,
  output S0
);

  wire and_1_out, and_2_out, and_3_out, and_4_out, and_5_out, and_6_out, and_7_out, and_8_out, and_9_out,
       and_10_out, and_11_out, and_12_out, and_13_out, and_14_out, not_1_out, not_2_out, not_3_out,
       not_4_out, not_5_out, not_6_out, not_7_out, not_8_out, not_9_out, not_10_out, not_11_out;

  not not_1 (not_1_out, Q3);
  not not_2 (not_2_out, Q2);
  not not_3 (not_3_out, Q1);
  not not_4 (not_4_out, Q0);
  not not_5 (not_5_out, Q1);
  not not_6 (not_6_out, Q0);
  not not_7 (not_7_out, Q1);
  not not_8 (not_8_out, Q0);
  not not_9 (not_9_out, Q1);
  not not_10 (not_10_out, Q0);
  not not_11 (not_11_out, Q0);
  and and_1 (and_1_out, Q3, Q1);
  and and_2 (and_2_out, Q3, Q2);
  and and_3 (and_3_out, not_1_out, not_2_out, not_3_out, not_4_out);
  and and_4 (and_4_out, Q3, Q0);
  and and_5 (and_5_out, Q3, Q1);
  and and_6 (and_6_out, Q3, Q2);
  and and_7 (and_7_out, Q2, Q0);
  and and_8 (and_8_out, Q2, Q1);
  and and_9 (and_9_out, Q3, not_5_out, not_6_out);
  and and_10 (and_10_out, Q3, Q1, Q0);
  and and_11 (and_11_out, Q1, Q0);
  and and_12 (and_12_out, Q2, not_7_out, not_8_out);
  and and_13 (and_13_out, Q3, not_9_out, not_10_out);
  and and_14 (and_14_out, Q3, Q2);
  or or_1 (S0, not_11_out, and_1_out, and_2_out);
  or or_2 (S3, and_3_out, and_4_out, and_5_out, and_6_out);
  or or_3 (S2, and_7_out, and_8_out, and_9_out, and_10_out);
  or or_4 (S1, and_11_out, and_12_out, and_13_out, and_14_out);
endmodule

module core_v8_nitro (
  input  gerar,
  input  confirmar_a,
  input  [3:0] a,
  input  swap_a,
  input  confirmar_b,
  input  reset_placar,
  input  [3:0] b,
  input  swap_y__b,
  input  change_players,
  input  CONFIRMAR,
  input  \começar ,
  input  stop,
  output maior,
  output igual,
  output [3:0] current_xa,
  output menor,
  output [3:0] current_ya,
  output [3:0] placar_a,
  output jogador_a_venceu,
  output led,
  output [3:0] placar_b,
  output [3:0] current_xb,
  output empate,
  output [3:0] current_yb,
  output jogador_b_venceu,
  output stop_a_f,
  output stop_b_f
);

  wire and_3_out, and_4_out, d_ff_1_qn, not_1_out, t_ff_1_q, t_ff_2_q;
  wire [4:0] input_logic_1_saida, input_logic_2_saida, multiplexer_1_out, somador_1_out_3;
  wire [7:0] random_1_out;

  T_Flip_Flop t_ff_1 (.clk(\começar ), .T(1'b1), .Q(t_ff_1_q));  // open: Qn, preset, reset, en
  T_Flip_Flop t_ff_2 (.clk(stop), .T(1'b1), .Q(t_ff_2_q));  // open: Qn, preset, reset, en
  input_logic input_logic_1 (
    .confirmar(confirmar_a), .\input (a), .saida(input_logic_1_saida), .current_x(current_xa),
    .change(swap_a), .current_y(current_ya));
  input_logic input_logic_2 (
    .confirmar(confirmar_b), .\input (b), .saida(input_logic_2_saida), .current_x(current_xb),
    .change(swap_y__b), .current_y(current_yb));
  and and_1 (stop_a_f, ~t_ff_2_q, t_ff_1_q);  // AND_Gate
  and and_2 (stop_b_f, t_ff_1_q, t_ff_2_q);
  Multiplexer #(.width(5)) multiplexer_1 (
    .in0(input_logic_1_saida), .in1(input_logic_2_saida), .out(multiplexer_1_out), .sel(change_players),
    .en(not_1_out));
  Random random_1 (.clk(gerar), .out(random_1_out));  // open: next, clr
  somador somador_1 (.in_1(random_1_out[3:0]), .in_2(random_1_out[7:4]), .out_3(somador_1_out_3));
  D_Flip_Flop d_ff_1 (.clk(CONFIRMAR), .D(d_ff_1_qn), .Qn(d_ff_1_qn));  // open: Q, preset, en, reset
  not not_1 (not_1_out, d_ff_1_qn);
  Comparator #(.width(5)) comparator_1 (.a(somador_1_out_3), .b(multiplexer_1_out), .gt(maior), .eq(igual), .lt(menor));
  and and_3 (and_3_out, ~change_players, igual);  // AND_Gate
  and and_4 (and_4_out, change_players, igual);
  Counter #(.width(4), .max('hf)) counter_1 (
    .Q(placar_a), .clk(and_3_out), .clr(reset_placar));  // open: load, D, count, carry
  Counter #(.width(4), .max('hf)) counter_2 (
    .Q(placar_b), .clk(and_4_out), .clr(reset_placar));  // open: load, D, count, carry
  Comparator #(.width(4)) comparator_2 (.a(placar_a), .b(4'b1111), .eq(jogador_a_venceu));  // open: gt, lt
  Comparator #(.width(4)) comparator_3 (.a(placar_b), .b(4'b1111), .eq(jogador_b_venceu));  // open: gt, lt
  and and_5 (empate, jogador_a_venceu, jogador_b_venceu);

  assign led = change_players;
endmodule

module guil (
  input  dm,
  input  um,
  input  ds,
  input  us,
  output c,
  output b,
  output a
);

  and and_1 (c, um, ds, us);
  and and_2 (b, ds, us);

  assign a = us;
endmodule

module \não_apague  (
  input  [3:0] entrada,
  output sinal,
  output [3:0] saida
);

  wire and_2_out, and_3_out, and_4_out, and_5_out, and_6_out, and_7_out, and_8_out, not_1_out, not_2_out,
       not_3_out, not_4_out, not_5_out, not_6_out, not_7_out, not_8_out, not_9_out, not_10_out, not_11_out;

  not not_1 (not_1_out, entrada[2]);
  not not_2 (not_2_out, entrada[1]);
  not not_3 (not_3_out, entrada[0]);
  not not_4 (not_4_out, entrada[3]);
  not not_5 (not_5_out, entrada[1]);
  not not_6 (not_6_out, entrada[0]);
  not not_7 (not_7_out, entrada[2]);
  not not_8 (not_8_out, entrada[2]);
  not not_9 (not_9_out, entrada[3]);
  not not_10 (not_10_out, entrada[0]);
  not not_11 (not_11_out, entrada[1]);
  and and_1 (saida[3], entrada[3], not_1_out, not_2_out, not_3_out);
  and and_2 (and_2_out, not_4_out, entrada[2]);
  and and_3 (and_3_out, entrada[2], not_5_out, not_6_out);
  and and_4 (and_4_out, entrada[3], not_7_out, entrada[0]);
  and and_5 (and_5_out, entrada[3], not_8_out, entrada[1]);
  and and_6 (and_6_out, not_9_out, entrada[1]);
  and and_7 (and_7_out, entrada[1], not_10_out);
  and and_8 (and_8_out, entrada[3], not_11_out, entrada[0]);
  or or_1 (saida[2], and_2_out, and_3_out, and_4_out, and_5_out);
  or or_2 (saida[1], and_6_out, and_7_out, and_8_out);

  assign saida[0] = entrada[0];
  assign sinal = entrada[3];
endmodule

module somador (
  input  [3:0] in_1,
  input  [3:0] in_2,
  output [4:0] out_3
);

  wire \não_apague_1_sinal , \não_apague_2_sinal ;
  wire [3:0] \não_apague_1_saida , \não_apague_2_saida ;
  wire [4:0] bit_extender_1_out, bit_extender_2_out;

  Hex_Digit_Display hex_digit_display_1 (.value(\não_apague_1_saida ));  // open: dp
  LED led_1 (.in(\não_apague_1_sinal ));
  \não_apague  \não_apague_1  (.saida(\não_apague_1_saida ), .entrada(in_1), .sinal(\não_apague_1_sinal ));
  Hex_Digit_Display hex_digit_display_2 (.value(\não_apague_2_saida ));  // open: dp
  \não_apague  \não_apague_2  (.saida(\não_apague_2_saida ), .entrada(in_2), .sinal(\não_apague_2_sinal ));
  LED led_2 (.in(\não_apague_2_sinal ));
  assign bit_extender_1_out = {{1{in_1[3]}}, in_1};  // Bit_Extender bit_extender_1
  assign bit_extender_2_out = {{1{in_2[3]}}, in_2};  // Bit_Extender bit_extender_2
  Adder #(.width(5)) adder_1 (.a(bit_extender_1_out), .b(bit_extender_2_out), .out(out_3));  // open: cin, cout
endmodule

module placar_a (
  input  placar_reset,
  input  count,
  output [3:0] TUS
);

  wire cont_placar_1_d2, cont_placar_1_f, cont_placar_1_g, cont_placar_1_s;
  wire [3:0] undriven;

  D_Flip_Flop d_ff_1 (
    .clk(count), .D(cont_placar_1_s), .Q(TUS[3]), .preset(undriven[3]), .reset(placar_reset));  // open: Qn, en
  D_Flip_Flop d_ff_2 (.clk(count), .D(cont_placar_1_d2), .Q(TUS[2]), .preset(undriven[2]));  // open: Qn, en, reset
  D_Flip_Flop d_ff_3 (
    .clk(count), .D(cont_placar_1_f), .Q(TUS[1]), .preset(undriven[1]), .reset(placar_reset));  // open: Qn, en
  D_Flip_Flop d_ff_4 (
    .clk(count), .D(cont_placar_1_g), .Q(TUS[0]), .preset(undriven[0]), .reset(placar_reset));  // open: Qn, en
  cont_placar cont_placar_1 (
    .a(TUS[3]), .b(TUS[2]), .c(TUS[1]), .d(TUS[0]), .s(cont_placar_1_s), .d2(cont_placar_1_d2),
    .f(cont_placar_1_f), .g(cont_placar_1_g));
  Hex_Digit_Display hex_digit_display_1 (.value(TUS));  // open: dp
endmodule

module cont_placar (
  input  a,
  input  b,
  input  c,
  input  d,
  output s,
  output d2,
  output f,
  output g
);

  wire and_1_out, and_2_out, and_3_out, and_4_out, and_5_out, and_6_out, and_7_out, and_8_out, and_9_out,
       and_10_out, not_1_out, not_2_out, not_3_out, not_4_out, not_5_out, not_6_out, not_7_out, not_8_out,
       not_9_out, not_10_out, not_11_out, not_12_out;

  not not_1 (not_1_out, a);
  not not_2 (not_2_out, b);
  not not_3 (not_3_out, c);
  not not_4 (not_4_out, d);
  not not_5 (not_5_out, b);
  and and_1 (and_1_out, not_5_out, c, d);
  and and_2 (and_2_out, b, not_6_out);
  not not_6 (not_6_out, c);
  and and_3 (and_3_out, b, not_7_out);
  not not_7 (not_7_out, d);
  not not_8 (not_8_out, c);
  and and_4 (and_4_out, not_8_out, d);
  not not_9 (not_9_out, a);
  and and_5 (and_5_out, not_9_out, c, not_10_out);
  not not_10 (not_10_out, d);
  not not_11 (not_11_out, b);
  and and_6 (and_6_out, not_11_out, c, not_12_out);
  not not_12 (not_12_out, d);
  not not_13 (g, d);
  and and_7 (and_7_out, not_1_out, b, c, d);
  and and_8 (and_8_out, a, not_2_out);
  and and_9 (and_9_out, a, not_3_out);
  and and_10 (and_10_out, a, not_4_out);
  or or_1 (d2, and_1_out, and_2_out, and_3_out);
  or or_2 (f, and_4_out, and_5_out, and_6_out);
  or or_3 (s, and_7_out, and_8_out, and_9_out, and_10_out);
endmodule

module input_logic (
  input  confirmar,
  input  [3:0] \input ,
  input  change,
  output [3:0] current_x,
  output [4:0] saida,
  output [3:0] current_y
);

  wire d_ff_1_q, d_ff_1_qn, demultiplexer_1_out0, demultiplexer_1_out1;
  wire [3:0] demultiplexer_2_out0, demultiplexer_2_out1;

  D_Flip_Flop d_ff_1 (.clk(confirmar), .D(d_ff_1_qn), .Q(d_ff_1_q), .Qn(d_ff_1_qn));  // open: preset, en, reset
  Demultiplexer #(.enable("false")) demultiplexer_1 (
    .out0(demultiplexer_1_out0), .out1(demultiplexer_1_out1), .in(d_ff_1_q), .sel(change));
  Demultiplexer #(.width(4), .enable("false")) demultiplexer_2 (
    .out0(demultiplexer_2_out0), .out1(demultiplexer_2_out1), .in(\input ), .sel(change));
  input_logic_2 input_logic_2_1 (.ada(demultiplexer_1_out0), .\inháme (demultiplexer_2_out0), .current(current_x));
  input_logic_2 input_logic_2_2 (.ada(demultiplexer_1_out1), .\inháme (demultiplexer_2_out1), .current(current_y));
  somador somador_1 (.in_1(current_x), .in_2(current_y), .out_3(saida));
endmodule

module input_logic_2 (
  input  ada,
  input  [3:0] \inháme ,
  output [3:0] current
);

  D_Flip_Flop d_ff_1 (.clk(ada), .D(\inháme [0]), .Q(current[0]));  // open: Qn, preset, en, reset
  D_Flip_Flop d_ff_2 (.clk(ada), .D(\inháme [1]), .Q(current[1]));  // open: Qn, preset, en, reset
  D_Flip_Flop d_ff_3 (.clk(ada), .D(\inháme [2]), .Q(current[2]));  // open: Qn, preset, en, reset
  D_Flip_Flop d_ff_4 (.clk(ada), .D(\inháme [3]), .Q(current[3]));  // open: Qn, preset, en, reset
endmodule

module placar_b (
  input  placar_reset,
  input  count,
  output [3:0] TUS
);

  wire cont_placar_1_d2, cont_placar_1_f, cont_placar_1_g, cont_placar_1_s;
  wire [3:0] undriven;

  D_Flip_Flop d_ff_1 (
    .clk(count), .D(cont_placar_1_s), .Q(TUS[3]), .preset(undriven[3]), .reset(placar_reset));  // open: Qn, en
  D_Flip_Flop d_ff_2 (.clk(count), .D(cont_placar_1_d2), .Q(TUS[2]), .preset(undriven[2]));  // open: Qn, en, reset
  D_Flip_Flop d_ff_3 (
    .clk(count), .D(cont_placar_1_f), .Q(TUS[1]), .preset(undriven[1]), .reset(placar_reset));  // open: Qn, en
  D_Flip_Flop d_ff_4 (
    .clk(count), .D(cont_placar_1_g), .Q(TUS[0]), .preset(undriven[0]), .reset(placar_reset));  // open: Qn, en
  cont_placar cont_placar_1 (
    .a(TUS[3]), .b(TUS[2]), .c(TUS[1]), .d(TUS[0]), .s(cont_placar_1_s), .d2(cont_placar_1_d2),
    .f(cont_placar_1_f), .g(cont_placar_1_g));
  Hex_Digit_Display hex_digit_display_1 (.value(TUS));  // open: dp
endmodule

module phineas (
  input  in_1
);

  D_Flip_Flop d_ff_1 (.clk(in_1));  // open: D, Q, Qn, preset, en, reset
  D_Flip_Flop d_ff_2 (.clk(in_1));  // open: D, Q, Qn, preset, en, reset
endmodule
